// Logisim project 3 bits divider.circ as structural Verilog
module main (
  input  [3:0] Dividendo,
  input  [3:0] Divisor
);


  // Other names for the same wires on the sheet: D[3:0] = Dividendo; Div[3:0] = Divisor
endmodule
