// Logisim project 3 bits multiplier.circ as structural Verilog: 5 circuits, main circuit main
module main (
  input  A,
  input  B,
  input  C,
  output Cout,
  output S
);

  wire and_1_out, and_2_out, and_3_out, xor_1_out;

  and and_1 (and_1_out, A, B);
  and and_2 (and_2_out, A, C);
  and and_3 (and_3_out, B, C);
  xor xor_1 (xor_1_out, B, C);
  xor xor_2 (S, xor_1_out, A);
  or or_1 (Cout, and_1_out, and_2_out, and_3_out);
endmodule

module Somador (
  input  [7:0] A,
  input  [7:0] B,
  input  C,
  output [7:0] out_4
);

  wire and_1_out, and_2_out, and_3_out, and_4_out, and_5_out, and_6_out, G0_out, G1_out, G2_out, or_1_out,
       or_2_out, or_3_out, P0_out, P1_out, P2_out;
  wire [7:0] xor_1_out;

  assign xor_1_out = B ^ {8{C}};  // XOR_Gate xor_1, 8 bits wide
  main main_1 (.A(A[0]), .B(xor_1_out[0]), .C(C));  // open: Cout, S
  or P0 (P0_out, xor_1_out[0], A[0]);
  and G0 (G0_out, xor_1_out[0], A[0]);
  or or_1 (or_1_out, G0_out, and_1_out);
  main main_2 (.A(xor_1_out[1]), .B(A[1]), .C(or_1_out));  // open: Cout, S
  and G1 (G1_out, xor_1_out[1], A[1]);
  and and_1 (and_1_out, P0_out, C);
  main main_3 (.A(xor_1_out[1]), .B(A[1]), .C(or_2_out));  // open: Cout, S
  or P1 (P1_out, xor_1_out[1], A[1]);
  and and_2 (and_2_out, C, G0_out, xor_1_out[1]);
  and and_3 (and_3_out, G0_out, P1_out);
  or or_2 (or_2_out, G1_out, and_3_out, and_2_out);
  or P2 (P2_out, xor_1_out[2], A[2]);
  and G2 (G2_out, xor_1_out[2], A[2]);
  and and_4 (and_4_out, P1_out, P2_out);
  or or_3 (or_3_out, G2_out, and_4_out, and_5_out, and_6_out);
  main main_4 (.A(xor_1_out[2]), .B(xor_1_out[2]), .C(or_3_out));  // open: Cout, S
  and and_5 (and_5_out, G0_out, P1_out, P2_out);
  and and_6 (and_6_out, C, P0_out, P1_out, P2_out);

  // Notes on the sheet:
  //   S0
  //   S1
  //   S2
endmodule

module multiplicador (
  input  A1,
  input  A0,
  input  A2,
  input  B2,
  input  B1,
  input  B0,
  output out_7,
  output out_8,
  output out_9,
  output out_10,
  output out_11,
  output out_12
);

  wire and_1_out, and_2_out, and_3_out, and_4_out, and_5_out, and_6_out, and_7_out, and_8_out,
       meio_somador_1_cout, meio_somador_1_s, meio_somador_2_cout, meio_somador_3_cout, somador_1bit_2_cout,
       somador_1bit_3_cout, somador_1bit_3_s;

  and and_1 (and_1_out, A2, B2);
  Hex_Digit_Display hex_digit_display_1 (.value({1'b0, A2, A1, A0}));  // open: dp
  Hex_Digit_Display hex_digit_display_2 (.value({1'b0, B2, B1, B0}));  // open: dp
  somador_1bit somador_1bit_1 (
    .a(meio_somador_1_cout), .b(and_1_out), .Cin(somador_1bit_2_cout), .S(out_8), .Cout(out_7));
  and and_2 (and_2_out, A2, B1);
  meio_somador meio_somador_1 (
    .a(somador_1bit_3_cout), .b(and_2_out), .s(meio_somador_1_s), .cout(meio_somador_1_cout));
  and and_3 (and_3_out, A1, B2);
  somador_1bit somador_1bit_2 (
    .a(meio_somador_1_s), .b(and_3_out), .Cin(meio_somador_2_cout), .S(out_9), .Cout(somador_1bit_2_cout));
  and and_4 (and_4_out, A2, B0);
  and and_5 (and_5_out, A1, B1);
  somador_1bit somador_1bit_3 (
    .a(and_4_out), .b(and_5_out), .Cin(meio_somador_3_cout), .S(somador_1bit_3_s), .Cout(somador_1bit_3_cout));
  and and_6 (and_6_out, A0, B2);
  meio_somador meio_somador_2 (.a(somador_1bit_3_s), .b(and_6_out), .s(out_10), .cout(meio_somador_2_cout));
  and and_7 (and_7_out, A1, B0);
  and and_8 (and_8_out, A0, B1);
  meio_somador meio_somador_3 (.a(and_7_out), .b(and_8_out), .s(out_11), .cout(meio_somador_3_cout));
  and and_9 (out_12, A0, B0);

  // Notes on the sheet:
  //   x
endmodule

module somador_1bit (
  input  a,
  input  b,
  input  Cin,
  output S,
  output Cout
);

  wire and_1_out, and_2_out, and_3_out, and_4_out, and_5_out, and_6_out, and_7_out, not_1_out, not_2_out,
       not_3_out, not_4_out, not_5_out, not_6_out;

  not not_1 (not_1_out, a);
  not not_2 (not_2_out, b);
  not not_3 (not_3_out, a);
  not not_4 (not_4_out, Cin);
  not not_5 (not_5_out, b);
  not not_6 (not_6_out, Cin);
  and and_1 (and_1_out, b, Cin);
  and and_2 (and_2_out, a, Cin);
  and and_3 (and_3_out, a, b);
  and and_4 (and_4_out, not_1_out, not_2_out, Cin);
  and and_5 (and_5_out, not_3_out, b, not_4_out);
  and and_6 (and_6_out, a, not_5_out, not_6_out);
  and and_7 (and_7_out, a, b, Cin);
  or or_1 (Cout, and_1_out, and_2_out, and_3_out);
  or or_2 (S, and_4_out, and_5_out, and_6_out, and_7_out);
endmodule

module meio_somador (
  input  a,
  input  b,
  output s,
  output cout
);

  wire and_2_out, and_3_out, not_1_out, not_2_out;

  not not_1 (not_1_out, a);
  not not_2 (not_2_out, b);
  and and_1 (cout, a, b);
  and and_2 (and_2_out, not_1_out, b);
  and and_3 (and_3_out, a, not_2_out);
  or or_1 (s, and_2_out, and_3_out);
endmodule
