// Logisim project 8 bits adder and subtractor lookahead .circ as structural Verilog: 2 circuits, main circuit main
module main (
  input  [7:0] A,
  input  [7:0] B,
  input  C,
  output [7:0] S
);

  wire and_1_out, and_2_out, and_3_out, and_4_out, and_5_out, and_6_out, and_7_out, and_8_out, and_9_out,
       and_10_out, and_11_out, and_12_out, and_13_out, and_14_out, and_15_out, and_16_out, and_17_out,
       and_18_out, and_19_out, and_20_out, and_21_out, and_23_out, and_24_out, and_25_out, and_26_out,
       and_27_out, B0, B1, B2, B3, B4, B5, B6, B7, G0, G1, G2, G3, G4, G5, G6, G7, or_1_out, or_2_out,
       or_3_out, or_4_out, or_5_out, or_6_out, or_7_out, P0, P1, P2, P3, P4, P5, P6, P7;

  assign {B7, B6, B5, B4, B3, B2, B1, B0} = B ^ {8{C}};  // XOR_Gate xor_1, 8 bits wide
  somador_1_bit somador_1_bit_1 (.A(A[0]), .B(B0), .Cin(C), .S(S[0]));
  and u_G0 (G0, A[0], B0);
  or u_P0 (P0, A[0], B0);
  somador_1_bit somador_1_bit_2 (.A(A[1]), .B(B1), .Cin(or_1_out), .S(S[1]));
  and u_G1 (G1, A[1], B1);
  or or_1 (or_1_out, G0, and_1_out);
  or u_P1 (P1, A[1], B1);
  and and_1 (and_1_out, P0, C);
  and and_2 (and_2_out, G0, P1);
  or or_2 (or_2_out, G1, and_2_out, and_3_out);
  somador_1_bit somador_1_bit_3 (.A(A[2]), .B(B2), .Cin(or_2_out), .S(S[2]));
  and u_G2 (G2, A[2], B2);
  and and_3 (and_3_out, P0, P1, C);
  or u_P2 (P2, A[2], B2);
  somador_1_bit somador_1_bit_4 (.A(A[3]), .B(B3), .Cin(or_3_out), .S(S[3]));
  and u_G3 (G3, A[3], B3);
  and and_4 (and_4_out, G1, P2);
  or or_3 (or_3_out, G2, and_4_out, and_5_out, and_6_out);
  or u_P3 (P3, A[3], B3);
  and and_5 (and_5_out, G0, P1, P2);
  and u_G4 (G4, A[4], B4);
  and and_6 (and_6_out, P0, P1, P2, C);
  or u_P4 (P4, A[4], B4);
  and and_7 (and_7_out, G2, P3);
  somador_1_bit somador_1_bit_5 (.A(A[4]), .B(B4), .Cin(or_4_out), .S(S[4]));
  and u_G5 (G5, A[5], B5);
  or or_4 (or_4_out, G3, and_7_out, and_8_out, and_9_out, and_10_out);
  or u_P5 (P5, A[5], B5);
  and and_8 (and_8_out, G1, P2, P3);
  and u_G6 (G6, A[6], B6);
  and and_9 (and_9_out, G0, P1, P2, P3);
  or u_P6 (P6, A[6], B6);
  and and_10 (and_10_out, P0, P1, P2, P3, C);
  and u_G7 (G7, A[7], B7);
  and and_11 (and_11_out, G3, P4);
  somador_1_bit somador_1_bit_6 (.A(A[5]), .B(B5), .Cin(or_5_out), .S(S[5]));
  or u_P7 (P7, A[7], B7);
  and and_12 (and_12_out, G2, P3, P4);
  or or_5 (or_5_out, G4, and_11_out, and_12_out, and_13_out, and_14_out, and_15_out);
  and and_13 (and_13_out, G1, P2, P3, P4);
  and and_14 (and_14_out, G0, P1, P2, P3, P4);
  and and_15 (and_15_out, P0, P1, P2, P3, P4, C);
  somador_1_bit somador_1_bit_7 (.A(A[6]), .B(B6), .Cin(or_6_out), .S(S[6]));
  and and_16 (and_16_out, G3, P4, P5);
  and and_17 (and_17_out, G4, P5);
  or or_6 (or_6_out, G5, and_17_out, and_16_out, and_18_out, and_19_out, and_20_out, and_21_out);
  and and_18 (and_18_out, G2, P3, P4, P5);
  and and_19 (and_19_out, G1, P2, P3, P4, P5);
  and and_20 (and_20_out, G0, P1, P2, P3, P4, P5);
  and and_21 (and_21_out, P0, P1, P2, P3, P4, P5, C);
  and and_22 (G6, G5, P6);
  somador_1_bit somador_1_bit_8 (.A(A[7]), .B(B7), .Cin(or_7_out), .S(S[7]));
  and and_23 (and_23_out, G4, P5, P6);
  and and_24 (and_24_out, G3, P4, P5, P6);
  or or_7 (or_7_out, G6, G6, and_23_out, and_24_out, and_25_out, and_26_out, and_27_out, and_27_out);
  and and_25 (and_25_out, G2, P3, P4, P5, P6);
  and and_26 (and_26_out, G1, P2, P3, P4, P5, P6);
  and and_27 (and_27_out, G0, P1, P2, P3, P4, P5, P6);
  and and_28 (and_27_out, P0, P1, P2, P3, P4, P5, P6, C);

  // Notes on the sheet:
  //   +
  //   =
endmodule

module somador_1_bit (
  input  A,
  input  B,
  input  Cin,
  output S
);

  wire xor_1_out;

  xor xor_1 (xor_1_out, Cin, B);
  xor xor_2 (S, xor_1_out, A);
endmodule
