// Logisim project 8 bits divider.circ as structural Verilog: 3 circuits, main circuit main
module main (
  input  [7:0] Dividendo,
  input  [7:0] Divisor,
  output [7:0] Resto,
  output [7:0] Quociente
);

  wire _0, _1, _2, _3, _4, _5, _6, _7;
  wire [7:0] multiplexer_1_out, multiplexer_2_out, multiplexer_3_out, multiplexer_4_out, multiplexer_5_out,
       multiplexer_6_out, multiplexer_7_out, somador_subtrator_1_s, somador_subtrator_2_s,
       somador_subtrator_3_s, somador_subtrator_4_s, somador_subtrator_5_s, somador_subtrator_6_s,
       somador_subtrator_7_s, somador_subtrator_8_s;

  not not_1 (Quociente[0], _0);
  not not_2 (Quociente[1], _1);
  not not_3 (Quociente[2], _2);
  not not_4 (Quociente[3], _3);
  not not_5 (Quociente[4], _4);
  not not_6 (Quociente[5], _5);
  not not_7 (Quociente[6], _6);
  not not_8 (Quociente[7], _7);
  Multiplexer #(.width(8), .enable("false")) multiplexer_1 (
    .in0(somador_subtrator_1_s), .in1({{7{1'b0}}, Dividendo[7]}), .out(multiplexer_1_out), .sel(_7));
  somador_subtrator somador_subtrator_1 (
    .A({{7{1'b0}}, Dividendo[7]}), .B(Divisor), .S(somador_subtrator_1_s), .C(1'b1), .bit_extra(_7));
  Multiplexer #(.width(8), .enable("false")) multiplexer_2 (
    .in0(somador_subtrator_2_s), .in1({multiplexer_1_out[6:0], Dividendo[6]}), .out(multiplexer_2_out),
    .sel(_6));
  somador_subtrator somador_subtrator_2 (
    .A({multiplexer_1_out[6:0], Dividendo[6]}), .B(Divisor), .S(somador_subtrator_2_s), .C(1'b1),
    .bit_extra(_6));
  somador_subtrator somador_subtrator_3 (
    .A({multiplexer_2_out[6:0], Dividendo[5]}), .B(Divisor), .S(somador_subtrator_3_s), .C(1'b1),
    .bit_extra(_5));
  Multiplexer #(.width(8), .enable("false")) multiplexer_3 (
    .in0(somador_subtrator_3_s), .in1({multiplexer_2_out[6:0], Dividendo[5]}), .out(multiplexer_3_out),
    .sel(_5));
  somador_subtrator somador_subtrator_4 (
    .A({multiplexer_3_out[6:0], Dividendo[4]}), .B(Divisor), .S(somador_subtrator_4_s), .C(1'b1),
    .bit_extra(_4));
  Multiplexer #(.width(8), .enable("false")) multiplexer_4 (
    .in0(somador_subtrator_4_s), .in1({multiplexer_3_out[6:0], Dividendo[4]}), .out(multiplexer_4_out),
    .sel(_4));
  somador_subtrator somador_subtrator_5 (
    .A({multiplexer_4_out[6:0], Dividendo[3]}), .B(Divisor), .S(somador_subtrator_5_s), .C(1'b1),
    .bit_extra(_3));
  Multiplexer #(.width(8), .enable("false")) multiplexer_5 (
    .in0(somador_subtrator_5_s), .in1({multiplexer_4_out[6:0], Dividendo[3]}), .out(multiplexer_5_out),
    .sel(_3));
  somador_subtrator somador_subtrator_6 (
    .A({multiplexer_5_out[6:0], Dividendo[2]}), .B(Divisor), .S(somador_subtrator_6_s), .C(1'b1),
    .bit_extra(_2));
  Multiplexer #(.width(8), .enable("false")) multiplexer_6 (
    .in0(somador_subtrator_6_s), .in1({multiplexer_5_out[6:0], Dividendo[2]}), .out(multiplexer_6_out),
    .sel(_2));
  Multiplexer #(.width(8), .enable("false")) multiplexer_7 (
    .in0(somador_subtrator_7_s), .in1({multiplexer_6_out[6:0], Dividendo[1]}), .out(multiplexer_7_out),
    .sel(_1));
  somador_subtrator somador_subtrator_7 (
    .A({multiplexer_6_out[6:0], Dividendo[1]}), .B(Divisor), .S(somador_subtrator_7_s), .C(1'b1),
    .bit_extra(_1));
  somador_subtrator somador_subtrator_8 (
    .A({multiplexer_7_out[6:0], Dividendo[0]}), .B(Divisor), .S(somador_subtrator_8_s), .C(1'b1),
    .bit_extra(_0));
  Multiplexer #(.width(8), .enable("false")) multiplexer_8 (
    .in0(somador_subtrator_8_s), .in1({multiplexer_7_out[6:0], Dividendo[0]}), .out(Resto), .sel(_0));
endmodule

module somador_1_bit (
  input  A,
  input  B,
  input  Cin,
  output S
);

  wire xor_1_out;

  xor xor_1 (xor_1_out, Cin, B);
  xor xor_2 (S, xor_1_out, A);
endmodule

module somador_subtrator (
  input  [7:0] A,
  input  [7:0] B,
  input  C,
  output [7:0] S,
  output bit_extra
);

  wire and_1_out, and_2_out, and_3_out, and_4_out, and_5_out, and_6_out, and_7_out, and_8_out, and_9_out,
       and_10_out, and_11_out, and_12_out, and_13_out, and_14_out, and_15_out, and_16_out, and_17_out,
       and_18_out, and_19_out, and_20_out, and_21_out, and_22_out, and_23_out, and_24_out, and_25_out,
       and_26_out, and_27_out, and_28_out, B0, B1, B2, B3, B4, B5, B6, B7, G0, G1, G2, G3, G4, G5, G6, G7,
       or_1_out, or_2_out, or_3_out, or_4_out, or_5_out, or_6_out, or_7_out, P0, P1, P2, P3, P4, P5, P6, P7;

  assign {B7, B6, B5, B4, B3, B2, B1, B0} = B ^ {8{C}};  // XOR_Gate xor_1, 8 bits wide
  somador_1_bit somador_1_bit_1 (.A(A[0]), .B(B0), .Cin(C), .S(S[0]));
  and u_G0 (G0, A[0], B0);
  or u_P0 (P0, A[0], B0);
  somador_1_bit somador_1_bit_2 (.A(A[1]), .B(B1), .Cin(or_1_out), .S(S[1]));
  and u_G1 (G1, A[1], B1);
  or or_1 (or_1_out, G0, and_1_out);
  or u_P1 (P1, A[1], B1);
  and and_1 (and_1_out, P0, C);
  and and_2 (and_2_out, G0, P1);
  or or_2 (or_2_out, G1, and_2_out, and_3_out);
  somador_1_bit somador_1_bit_3 (.A(A[2]), .B(B2), .Cin(or_2_out), .S(S[2]));
  and u_G2 (G2, A[2], B2);
  and and_3 (and_3_out, P0, P1, C);
  or u_P2 (P2, A[2], B2);
  somador_1_bit somador_1_bit_4 (.A(A[3]), .B(B3), .Cin(or_3_out), .S(S[3]));
  and u_G3 (G3, A[3], B3);
  and and_4 (and_4_out, G1, P2);
  or or_3 (or_3_out, G2, and_4_out, and_5_out, and_6_out);
  or u_P3 (P3, A[3], B3);
  and and_5 (and_5_out, G0, P1, P2);
  and u_G4 (G4, A[4], B4);
  and and_6 (and_6_out, P0, P1, P2, C);
  or u_P4 (P4, A[4], B4);
  and and_7 (and_7_out, G2, P3);
  somador_1_bit somador_1_bit_5 (.A(A[4]), .B(B4), .Cin(or_4_out), .S(S[4]));
  and u_G5 (G5, A[5], B5);
  or or_4 (or_4_out, G3, and_7_out, and_8_out, and_9_out, and_10_out);
  or u_P5 (P5, A[5], B5);
  and and_8 (and_8_out, G1, P2, P3);
  and u_G6 (G6, A[6], B6);
  and and_9 (and_9_out, G0, P1, P2, P3);
  or u_P6 (P6, A[6], B6);
  and and_10 (and_10_out, P0, P1, P2, P3, C);
  and u_G7 (G7, A[7], B7);
  and and_11 (and_11_out, G3, P4);
  somador_1_bit somador_1_bit_6 (.A(A[5]), .B(B5), .Cin(or_5_out), .S(S[5]));
  or u_P7 (P7, A[7], B7);
  and and_12 (and_12_out, G2, P3, P4);
  or or_5 (or_5_out, G4, and_11_out, and_12_out, and_13_out, and_14_out, and_15_out);
  and and_13 (and_13_out, G1, P2, P3, P4);
  and and_14 (and_14_out, G0, P1, P2, P3, P4);
  and and_15 (and_15_out, P0, P1, P2, P3, P4, C);
  somador_1_bit somador_1_bit_7 (.A(A[6]), .B(B6), .Cin(or_6_out), .S(S[6]));
  and and_16 (and_16_out, G3, P4, P5);
  and and_17 (and_17_out, G4, P5);
  or or_6 (or_6_out, G5, and_17_out, and_16_out, and_18_out, and_19_out, and_20_out, and_21_out);
  and and_18 (and_18_out, G2, P3, P4, P5);
  and and_19 (and_19_out, G1, P2, P3, P4, P5);
  and and_20 (and_20_out, G0, P1, P2, P3, P4, P5);
  and and_21 (and_21_out, P0, P1, P2, P3, P4, P5, C);
  and and_22 (and_22_out, G5, P6);
  somador_1_bit somador_1_bit_8 (.A(A[7]), .B(B7), .Cin(or_7_out), .S(bit_extra));
  and and_23 (and_23_out, G4, P5, P6);
  and and_24 (and_24_out, G3, P4, P5, P6);
  or or_7 (or_7_out, G6, and_22_out, and_23_out, and_24_out, and_25_out, and_26_out, and_27_out, and_28_out);
  and and_25 (and_25_out, G2, P3, P4, P5, P6);
  and and_26 (and_26_out, G1, P2, P3, P4, P5, P6);
  and and_27 (and_27_out, G0, P1, P2, P3, P4, P5, P6);
  and and_28 (and_28_out, P0, P1, P2, P3, P4, P5, P6, C);

  assign S[7] = bit_extra;

  // Notes on the sheet:
  //   +
  //   =
endmodule
