// Logisim project 8 bits memory.circ as structural Verilog: 2 circuits, main circuit main
module main (
  input  [7:0] in_1,
  input  in_2,
  input  in_3,
  input  in_4,
  input  in_5,
  output out_6,
  output out_7,
  output out_8
);

  wire and_1_out, and_2_out, and_3_out, and_4_out, and_5_out, and_6_out, and_7_out, and_8_out, and_9_out,
       and_10_out, and_11_out, and_12_out, and_13_out, and_14_out, and_15_out, and_16_out, and_17_out,
       and_18_out, and_19_out, and_20_out, and_21_out, and_22_out, and_23_out, and_24_out, and_25_out,
       and_26_out, and_27_out, and_28_out, and_29_out, and_30_out, and_31_out, and_32_out, and_33_out,
       and_34_out, and_35_out, and_36_out, and_37_out, and_38_out, and_39_out, and_40_out, d_ff_1_q,
       d_ff_2_q, d_ff_3_q, d_ff_4_q, d_ff_5_q, d_ff_6_q, d_ff_8_q, d_ff_9_q, d_ff_10_q, d_ff_11_q, d_ff_12_q,
       d_ff_13_q, d_ff_14_q, d_ff_16_q, d_ff_17_q, d_ff_18_q, d_ff_19_q, d_ff_20_q, d_ff_21_q, d_ff_22_q,
       d_ff_24_q;

  and and_1 (and_1_out, ~in_3, ~in_4, ~in_5);  // AND_Gate
  and and_2 (and_2_out, ~in_3, ~in_4, in_5);  // AND_Gate
  and and_3 (and_3_out, ~in_3, in_4, ~in_5);  // AND_Gate
  and and_4 (and_4_out, ~in_3, in_4, in_5);  // AND_Gate
  and and_5 (and_5_out, in_3, ~in_4, ~in_5);  // AND_Gate
  and and_6 (and_6_out, in_3, ~in_4, in_5);  // AND_Gate
  and and_7 (and_7_out, in_3, in_4, ~in_5);  // AND_Gate
  and and_8 (and_8_out, in_3, in_4, in_5);
  and and_9 (and_9_out, and_1_out, in_2);
  and and_10 (and_10_out, and_2_out, in_2);
  and and_11 (and_11_out, and_3_out, in_2);
  and and_12 (and_12_out, and_4_out, in_2);
  and and_13 (and_13_out, and_5_out, in_2);
  and and_14 (and_14_out, and_6_out, in_2);
  and and_15 (and_15_out, and_7_out, in_2);
  and and_16 (and_16_out, and_8_out, in_2);
  D_Flip_Flop d_ff_1 (.clk(and_9_out), .D(in_1[7]), .Q(d_ff_1_q));  // open: Qn, preset, en, reset
  and and_17 (and_17_out, d_ff_1_q, and_1_out);
  D_Flip_Flop d_ff_2 (.clk(and_10_out), .D(in_1[7]), .Q(d_ff_2_q));  // open: Qn, preset, en, reset
  D_Flip_Flop d_ff_3 (.clk(and_11_out), .D(in_1[7]), .Q(d_ff_3_q));  // open: Qn, preset, en, reset
  D_Flip_Flop d_ff_4 (.clk(and_12_out), .D(in_1[7]), .Q(d_ff_4_q));  // open: Qn, preset, en, reset
  D_Flip_Flop d_ff_5 (.clk(and_13_out), .D(in_1[7]), .Q(d_ff_5_q));  // open: Qn, preset, en, reset
  D_Flip_Flop d_ff_6 (.clk(and_14_out), .D(in_1[7]), .Q(d_ff_6_q));  // open: Qn, preset, en, reset
  D_Flip_Flop d_ff_7 (.clk(and_15_out), .D(in_1[7]), .Q(and_7_out));  // open: Qn, preset, en, reset
  D_Flip_Flop d_ff_8 (.clk(and_16_out), .D(in_1[7]), .Q(d_ff_8_q));  // open: Qn, preset, en, reset
  and and_18 (and_18_out, d_ff_2_q, and_2_out);
  and and_19 (and_19_out, d_ff_5_q, and_5_out);
  or or_1 (out_6, and_17_out, and_18_out, and_20_out, and_23_out, and_19_out, and_21_out, and_22_out, and_24_out);
  and and_20 (and_20_out, d_ff_3_q, and_3_out);
  and and_21 (and_21_out, d_ff_6_q, and_6_out);
  and and_22 (and_22_out, and_7_out, and_7_out);
  and and_23 (and_23_out, d_ff_4_q, and_12_out);
  and and_24 (and_24_out, d_ff_8_q, and_8_out);
  D_Flip_Flop d_ff_9 (.clk(and_9_out), .D(in_1[6]), .Q(d_ff_9_q));  // open: Qn, preset, en, reset
  D_Flip_Flop d_ff_10 (.clk(and_10_out), .D(in_1[6]), .Q(d_ff_10_q));  // open: Qn, preset, en, reset
  D_Flip_Flop d_ff_11 (.clk(and_11_out), .D(in_1[6]), .Q(d_ff_11_q));  // open: Qn, preset, en, reset
  D_Flip_Flop d_ff_12 (.clk(and_12_out), .D(in_1[6]), .Q(d_ff_12_q));  // open: Qn, preset, en, reset
  D_Flip_Flop d_ff_13 (.clk(and_13_out), .D(in_1[6]), .Q(d_ff_13_q));  // open: Qn, preset, en, reset
  D_Flip_Flop d_ff_14 (.clk(and_14_out), .D(in_1[6]), .Q(d_ff_14_q));  // open: Qn, preset, en, reset
  D_Flip_Flop d_ff_15 (.clk(and_15_out), .D(in_1[6]), .Q(and_7_out));  // open: Qn, preset, en, reset
  D_Flip_Flop d_ff_16 (.clk(and_16_out), .D(in_1[6]), .Q(d_ff_16_q));  // open: Qn, preset, en, reset
  and and_25 (and_25_out, d_ff_9_q, and_1_out);
  and and_26 (and_26_out, d_ff_10_q, and_2_out);
  and and_27 (and_27_out, d_ff_11_q, and_3_out);
  and and_28 (and_28_out, d_ff_12_q, and_4_out);
  and and_29 (and_29_out, d_ff_13_q, and_5_out);
  or or_2 (out_7, and_25_out, and_26_out, and_27_out, and_28_out, and_29_out, and_30_out, and_31_out, and_32_out);
  and and_30 (and_30_out, d_ff_14_q, and_6_out);
  and and_31 (and_31_out, and_7_out, and_7_out);
  and and_32 (and_32_out, d_ff_16_q, and_8_out);
  D_Flip_Flop d_ff_17 (.clk(and_9_out), .D(in_1[5]), .Q(d_ff_17_q));  // open: Qn, preset, en, reset
  D_Flip_Flop d_ff_18 (.clk(and_10_out), .D(in_1[5]), .Q(d_ff_18_q));  // open: Qn, preset, en, reset
  D_Flip_Flop d_ff_19 (.clk(and_11_out), .D(in_1[5]), .Q(d_ff_19_q));  // open: Qn, preset, en, reset
  D_Flip_Flop d_ff_20 (.clk(and_12_out), .D(in_1[5]), .Q(d_ff_20_q));  // open: Qn, preset, en, reset
  D_Flip_Flop d_ff_21 (.clk(and_13_out), .D(in_1[5]), .Q(d_ff_21_q));  // open: Qn, preset, en, reset
  D_Flip_Flop d_ff_22 (.clk(and_14_out), .D(in_1[5]), .Q(d_ff_22_q));  // open: Qn, preset, en, reset
  D_Flip_Flop d_ff_23 (.clk(and_15_out), .D(in_1[5]), .Q(and_7_out));  // open: Qn, preset, en, reset
  D_Flip_Flop d_ff_24 (.clk(and_16_out), .D(in_1[5]), .Q(d_ff_24_q));  // open: Qn, preset, en, reset
  and and_33 (and_33_out, d_ff_17_q, and_1_out);
  and and_34 (and_34_out, d_ff_18_q, and_2_out);
  and and_35 (and_35_out, d_ff_19_q, and_3_out);
  and and_36 (and_36_out, d_ff_20_q, and_4_out);
  and and_37 (and_37_out, d_ff_21_q, and_5_out);
  and and_38 (and_38_out, d_ff_22_q, and_6_out);
  or or_3 (out_8, and_33_out, and_34_out, and_35_out, and_36_out, and_37_out, and_38_out, and_39_out, and_40_out);
  and and_39 (and_39_out, and_7_out, and_7_out);
  and and_40 (and_40_out, d_ff_24_q, and_8_out);
endmodule

module memoria (
  input  [7:0] in_1,
  input  in_2,
  input  in_3,
  input  in_4,
  input  in_5
);

  wire and_1_out, and_2_out, and_3_out, and_4_out, and_5_out, and_6_out, and_7_out, and_8_out, and_16_out;

  and and_1 (and_1_out, ~in_3, ~in_4, ~in_5);  // AND_Gate
  and and_2 (and_2_out, ~in_3, ~in_4, in_5);  // AND_Gate
  and and_3 (and_3_out, ~in_3, in_4, ~in_5);  // AND_Gate
  and and_4 (and_4_out, ~in_3, in_4, in_5);  // AND_Gate
  and and_5 (and_5_out, in_3, ~in_4, ~in_5);  // AND_Gate
  and and_6 (and_6_out, in_3, ~in_4, in_5);  // AND_Gate
  and and_7 (and_7_out, in_3, in_4, ~in_5);  // AND_Gate
  and and_8 (and_8_out, in_3, in_4, in_5);
  // AND_Gate and_9 has open pins: in0=and_1_out, in1=in_2, out=open
  // AND_Gate and_10 has open pins: in0=and_2_out, in1=in_2, out=open
  // AND_Gate and_11 has open pins: in0=and_3_out, in1=in_2, out=open
  // AND_Gate and_12 has open pins: in0=and_4_out, in1=in_2, out=open
  // AND_Gate and_13 has open pins: in0=and_5_out, in1=in_2, out=open
  // AND_Gate and_14 has open pins: in0=and_6_out, in1=in_2, out=open
  // AND_Gate and_15 has open pins: in0=and_7_out, in1=in_2, out=open
  and and_16 (and_16_out, and_8_out, in_2);
endmodule
