// Logisim project 8 bits multiplier.circ as structural Verilog: 5 circuits, main circuit main
module main (
  input  A,
  input  B,
  input  C,
  output Cout,
  output S
);

  wire and_1_out, and_2_out, and_3_out, xor_1_out;

  and and_1 (and_1_out, A, B);
  and and_2 (and_2_out, A, C);
  and and_3 (and_3_out, B, C);
  xor xor_1 (xor_1_out, B, C);
  xor xor_2 (S, xor_1_out, A);
  or or_1 (Cout, and_1_out, and_2_out, and_3_out);
endmodule

module Somador (
  input  [7:0] A,
  input  [7:0] B,
  input  C,
  output [7:0] out_4
);

  wire and_1_out, and_2_out, and_3_out, and_4_out, and_5_out, and_6_out, G0_out, G1_out, G2_out, or_1_out,
       or_2_out, or_3_out, P0_out, P1_out, P2_out;
  wire [7:0] xor_1_out;

  assign xor_1_out = B ^ {8{C}};  // XOR_Gate xor_1, 8 bits wide
  main main_1 (.A(A[0]), .B(xor_1_out[0]), .C(C));  // open: Cout, S
  and G0 (G0_out, xor_1_out[0], A[0]);
  or P0 (P0_out, xor_1_out[0], A[0]);
  or or_1 (or_1_out, G0_out, and_1_out);
  main main_2 (.A(xor_1_out[1]), .B(A[1]), .C(or_1_out));  // open: Cout, S
  and G1 (G1_out, xor_1_out[1], A[1]);
  and and_1 (and_1_out, P0_out, C);
  main main_3 (.A(xor_1_out[1]), .B(A[1]), .C(or_2_out));  // open: Cout, S
  or P1 (P1_out, xor_1_out[1], A[1]);
  and and_2 (and_2_out, G0_out, P1_out);
  and and_3 (and_3_out, C, G0_out, xor_1_out[1]);
  or or_2 (or_2_out, G1_out, and_2_out, and_3_out);
  or P2 (P2_out, xor_1_out[2], A[2]);
  and G2 (G2_out, xor_1_out[2], A[2]);
  and and_4 (and_4_out, P1_out, P2_out);
  or or_3 (or_3_out, G2_out, and_4_out, and_5_out, and_6_out);
  main main_4 (.A(xor_1_out[2]), .B(xor_1_out[2]), .C(or_3_out));  // open: Cout, S
  and and_5 (and_5_out, G0_out, P1_out, P2_out);
  and and_6 (and_6_out, C, P0_out, P1_out, P2_out);

  // Notes on the sheet:
  //   S0
  //   S1
  //   S2
endmodule

module multiplicador (
  input  [7:0] A,
  input  [7:0] B,
  output [15:0] saida
);

  wire and_1_out, and_2_out, and_3_out, and_4_out, and_5_out, and_6_out, and_7_out, and_8_out, and_9_out,
       and_10_out, and_11_out, and_12_out, and_13_out, and_14_out, and_15_out, and_16_out, and_17_out,
       and_18_out, and_19_out, and_20_out, and_21_out, and_22_out, and_23_out, and_24_out, and_25_out,
       and_26_out, and_27_out, and_28_out, and_29_out, and_30_out, and_31_out, and_32_out, and_33_out,
       and_34_out, and_35_out, and_36_out, and_37_out, and_38_out, and_39_out, and_40_out, and_41_out,
       and_42_out, and_43_out, and_44_out, and_45_out, and_46_out, and_47_out, and_48_out, and_49_out,
       and_50_out, and_51_out, and_52_out, and_53_out, and_54_out, and_55_out, and_56_out, and_57_out,
       and_58_out, and_59_out, and_60_out, and_61_out, and_62_out, and_63_out, meio_somador_1_cout,
       meio_somador_1_s, meio_somador_2_cout, meio_somador_3_cout, meio_somador_4_cout, meio_somador_5_cout,
       meio_somador_6_cout, meio_somador_7_cout, meio_somador_8_cout, somador_1bit_2_cout, somador_1bit_2_s,
       somador_1bit_3_cout, somador_1bit_4_cout, somador_1bit_4_s, somador_1bit_5_cout, somador_1bit_6_cout,
       somador_1bit_6_s, somador_1bit_7_cout, somador_1bit_7_s, somador_1bit_8_cout, somador_1bit_9_cout,
       somador_1bit_9_s, somador_1bit_10_cout, somador_1bit_10_s, somador_1bit_11_cout, somador_1bit_12_cout,
       somador_1bit_12_s, somador_1bit_13_cout, somador_1bit_13_s, somador_1bit_14_cout, somador_1bit_14_s,
       somador_1bit_15_cout, somador_1bit_15_s, somador_1bit_16_cout, somador_1bit_17_cout,
       somador_1bit_17_s, somador_1bit_18_cout, somador_1bit_18_s, somador_1bit_19_cout, somador_1bit_19_s,
       somador_1bit_20_cout, somador_1bit_20_s, somador_1bit_21_cout, somador_1bit_21_s,
       somador_1bit_22_cout, somador_1bit_22_s, somador_1bit_23_cout, somador_1bit_23_s,
       somador_1bit_24_cout, somador_1bit_24_s, somador_1bit_25_cout, somador_1bit_25_s,
       somador_1bit_26_cout, somador_1bit_26_s, somador_1bit_27_cout, somador_1bit_28_cout,
       somador_1bit_28_s, somador_1bit_29_cout, somador_1bit_29_s, somador_1bit_30_cout, somador_1bit_30_s,
       somador_1bit_31_cout, somador_1bit_31_s, somador_1bit_32_cout, somador_1bit_32_s,
       somador_1bit_33_cout, somador_1bit_33_s, somador_1bit_34_cout, somador_1bit_34_s,
       somador_1bit_35_cout, somador_1bit_35_s, somador_1bit_36_cout, somador_1bit_36_s,
       somador_1bit_37_cout, somador_1bit_37_s, somador_1bit_38_cout, somador_1bit_38_s,
       somador_1bit_39_cout, somador_1bit_39_s, somador_1bit_40_cout, somador_1bit_40_s,
       somador_1bit_41_cout, somador_1bit_41_s, somador_1bit_42_cout, somador_1bit_42_s,
       somador_1bit_43_cout, somador_1bit_43_s, somador_1bit_44_cout, somador_1bit_44_s,
       somador_1bit_45_cout, somador_1bit_45_s, somador_1bit_46_cout, somador_1bit_46_s,
       somador_1bit_47_cout, somador_1bit_47_s, somador_1bit_48_cout, somador_1bit_48_s;

  and and_1 (and_1_out, A[7], B[7]);
  somador_1bit somador_1bit_1 (
    .a(somador_1bit_2_cout), .b(and_1_out), .Cin(somador_1bit_3_cout), .S(saida[14]), .Cout(saida[15]));
  and and_2 (and_2_out, A[7], B[6]);
  somador_1bit somador_1bit_2 (
    .a(somador_1bit_6_cout), .b(and_2_out), .Cin(somador_1bit_4_cout), .S(somador_1bit_2_s),
    .Cout(somador_1bit_2_cout));
  and and_3 (and_3_out, A[6], B[7]);
  somador_1bit somador_1bit_3 (
    .a(somador_1bit_2_s), .b(and_3_out), .Cin(somador_1bit_5_cout), .S(saida[13]), .Cout(somador_1bit_3_cout));
  and and_4 (and_4_out, A[7], B[5]);
  and and_5 (and_5_out, A[6], B[6]);
  somador_1bit somador_1bit_4 (
    .a(somador_1bit_6_s), .b(and_5_out), .Cin(somador_1bit_7_cout), .S(somador_1bit_4_s),
    .Cout(somador_1bit_4_cout));
  and and_6 (and_6_out, A[5], B[7]);
  somador_1bit somador_1bit_5 (
    .a(somador_1bit_4_s), .b(and_6_out), .Cin(somador_1bit_8_cout), .S(saida[12]), .Cout(somador_1bit_5_cout));
  and and_7 (and_7_out, A[7], B[4]);
  and and_8 (and_8_out, A[6], B[5]);
  somador_1bit somador_1bit_6 (
    .a(somador_1bit_9_cout), .b(and_4_out), .Cin(somador_1bit_10_cout), .S(somador_1bit_6_s),
    .Cout(somador_1bit_6_cout));
  and and_9 (and_9_out, A[5], B[6]);
  somador_1bit somador_1bit_7 (
    .a(somador_1bit_10_s), .b(and_9_out), .Cin(somador_1bit_15_cout), .S(somador_1bit_7_s),
    .Cout(somador_1bit_7_cout));
  and and_10 (and_10_out, A[4], B[7]);
  somador_1bit somador_1bit_8 (
    .a(somador_1bit_7_s), .b(and_10_out), .Cin(somador_1bit_11_cout), .S(saida[11]),
    .Cout(somador_1bit_8_cout));
  and and_11 (and_11_out, A[7], B[3]);
  and and_12 (and_12_out, A[6], B[4]);
  somador_1bit somador_1bit_9 (
    .a(somador_1bit_12_cout), .b(and_7_out), .Cin(somador_1bit_13_cout), .S(somador_1bit_9_s),
    .Cout(somador_1bit_9_cout));
  and and_13 (and_13_out, A[5], B[5]);
  somador_1bit somador_1bit_10 (
    .a(somador_1bit_9_s), .b(and_8_out), .Cin(somador_1bit_14_cout), .S(somador_1bit_10_s),
    .Cout(somador_1bit_10_cout));
  and and_14 (and_14_out, A[4], B[6]);
  and and_15 (and_15_out, A[3], B[7]);
  somador_1bit somador_1bit_11 (
    .a(somador_1bit_15_s), .b(and_15_out), .Cin(somador_1bit_16_cout), .S(saida[10]),
    .Cout(somador_1bit_11_cout));
  and and_16 (and_16_out, A[6], B[3]);
  somador_1bit somador_1bit_12 (
    .a(somador_1bit_17_cout), .b(and_11_out), .Cin(somador_1bit_18_cout), .S(somador_1bit_12_s),
    .Cout(somador_1bit_12_cout));
  somador_1bit somador_1bit_13 (
    .a(somador_1bit_12_s), .b(and_12_out), .Cin(somador_1bit_19_cout), .S(somador_1bit_13_s),
    .Cout(somador_1bit_13_cout));
  and and_17 (and_17_out, A[4], B[5]);
  somador_1bit somador_1bit_14 (
    .a(somador_1bit_13_s), .b(and_13_out), .Cin(somador_1bit_20_cout), .S(somador_1bit_14_s),
    .Cout(somador_1bit_14_cout));
  and and_18 (and_18_out, A[3], B[6]);
  somador_1bit somador_1bit_15 (
    .a(somador_1bit_14_s), .b(and_14_out), .Cin(somador_1bit_21_cout), .S(somador_1bit_15_s),
    .Cout(somador_1bit_15_cout));
  and and_19 (and_19_out, A[2], B[7]);
  somador_1bit somador_1bit_16 (
    .a(somador_1bit_21_s), .b(and_19_out), .Cin(somador_1bit_27_cout), .S(saida[9]),
    .Cout(somador_1bit_16_cout));
  and and_20 (and_20_out, A[7], B[2]);
  somador_1bit somador_1bit_17 (
    .a(meio_somador_1_cout), .b(and_20_out), .Cin(somador_1bit_22_cout), .S(somador_1bit_17_s),
    .Cout(somador_1bit_17_cout));
  somador_1bit somador_1bit_18 (
    .a(somador_1bit_17_s), .b(and_16_out), .Cin(somador_1bit_23_cout), .S(somador_1bit_18_s),
    .Cout(somador_1bit_18_cout));
  and and_21 (and_21_out, A[5], B[4]);
  somador_1bit somador_1bit_19 (
    .a(somador_1bit_18_s), .b(and_21_out), .Cin(somador_1bit_24_cout), .S(somador_1bit_19_s),
    .Cout(somador_1bit_19_cout));
  somador_1bit somador_1bit_20 (
    .a(somador_1bit_19_s), .b(and_17_out), .Cin(somador_1bit_25_cout), .S(somador_1bit_20_s),
    .Cout(somador_1bit_20_cout));
  and and_22 (and_22_out, A[2], B[6]);
  somador_1bit somador_1bit_21 (
    .a(somador_1bit_20_s), .b(and_18_out), .Cin(somador_1bit_26_cout), .S(somador_1bit_21_s),
    .Cout(somador_1bit_21_cout));
  and and_23 (and_23_out, A[1], B[7]);
  and and_24 (and_24_out, A[7], B[1]);
  meio_somador meio_somador_1 (
    .a(somador_1bit_28_cout), .b(and_24_out), .s(meio_somador_1_s), .cout(meio_somador_1_cout));
  and and_25 (and_25_out, A[6], B[2]);
  somador_1bit somador_1bit_22 (
    .a(meio_somador_1_s), .b(and_25_out), .Cin(somador_1bit_29_cout), .S(somador_1bit_22_s),
    .Cout(somador_1bit_22_cout));
  and and_26 (and_26_out, A[5], B[3]);
  somador_1bit somador_1bit_23 (
    .a(somador_1bit_22_s), .b(and_26_out), .Cin(somador_1bit_30_cout), .S(somador_1bit_23_s),
    .Cout(somador_1bit_23_cout));
  and and_27 (and_27_out, A[4], B[4]);
  somador_1bit somador_1bit_24 (
    .a(somador_1bit_23_s), .b(and_27_out), .Cin(somador_1bit_31_cout), .S(somador_1bit_24_s),
    .Cout(somador_1bit_24_cout));
  and and_28 (and_28_out, A[3], B[5]);
  somador_1bit somador_1bit_25 (
    .a(somador_1bit_24_s), .b(and_28_out), .Cin(somador_1bit_32_cout), .S(somador_1bit_25_s),
    .Cout(somador_1bit_25_cout));
  and and_29 (and_29_out, A[1], B[6]);
  somador_1bit somador_1bit_26 (
    .a(somador_1bit_25_s), .b(and_22_out), .Cin(somador_1bit_33_cout), .S(somador_1bit_26_s),
    .Cout(somador_1bit_26_cout));
  and and_30 (and_30_out, A[0], B[7]);
  somador_1bit somador_1bit_27 (
    .a(somador_1bit_26_s), .b(and_23_out), .Cin(meio_somador_2_cout), .S(saida[8]),
    .Cout(somador_1bit_27_cout));
  meio_somador meio_somador_2 (.a(somador_1bit_33_s), .b(and_30_out), .s(saida[7]), .cout(meio_somador_2_cout));
  and and_31 (and_31_out, A[7], B[0]);
  and and_32 (and_32_out, A[6], B[1]);
  somador_1bit somador_1bit_28 (
    .a(and_31_out), .b(and_32_out), .Cin(somador_1bit_34_cout), .S(somador_1bit_28_s),
    .Cout(somador_1bit_28_cout));
  and and_33 (and_33_out, A[5], B[2]);
  somador_1bit somador_1bit_29 (
    .a(somador_1bit_28_s), .b(and_33_out), .Cin(somador_1bit_35_cout), .S(somador_1bit_29_s),
    .Cout(somador_1bit_29_cout));
  and and_34 (and_34_out, A[4], B[3]);
  somador_1bit somador_1bit_30 (
    .a(somador_1bit_29_s), .b(and_34_out), .Cin(somador_1bit_36_cout), .S(somador_1bit_30_s),
    .Cout(somador_1bit_30_cout));
  and and_35 (and_35_out, A[3], B[4]);
  somador_1bit somador_1bit_31 (
    .a(somador_1bit_30_s), .b(and_35_out), .Cin(somador_1bit_37_cout), .S(somador_1bit_31_s),
    .Cout(somador_1bit_31_cout));
  and and_36 (and_36_out, A[2], B[5]);
  somador_1bit somador_1bit_32 (
    .a(somador_1bit_31_s), .b(and_36_out), .Cin(somador_1bit_38_cout), .S(somador_1bit_32_s),
    .Cout(somador_1bit_32_cout));
  somador_1bit somador_1bit_33 (
    .a(somador_1bit_32_s), .b(and_29_out), .Cin(meio_somador_3_cout), .S(somador_1bit_33_s),
    .Cout(somador_1bit_33_cout));
  and and_37 (and_37_out, A[6], B[0]);
  and and_38 (and_38_out, A[5], B[1]);
  somador_1bit somador_1bit_34 (
    .a(and_37_out), .b(and_38_out), .Cin(somador_1bit_39_cout), .S(somador_1bit_34_s),
    .Cout(somador_1bit_34_cout));
  and and_39 (and_39_out, A[4], B[2]);
  somador_1bit somador_1bit_35 (
    .a(somador_1bit_34_s), .b(and_39_out), .Cin(somador_1bit_40_cout), .S(somador_1bit_35_s),
    .Cout(somador_1bit_35_cout));
  and and_40 (and_40_out, A[3], B[3]);
  somador_1bit somador_1bit_36 (
    .a(somador_1bit_35_s), .b(and_40_out), .Cin(somador_1bit_41_cout), .S(somador_1bit_36_s),
    .Cout(somador_1bit_36_cout));
  and and_41 (and_41_out, A[2], B[4]);
  somador_1bit somador_1bit_37 (
    .a(somador_1bit_36_s), .b(and_41_out), .Cin(somador_1bit_42_cout), .S(somador_1bit_37_s),
    .Cout(somador_1bit_37_cout));
  and and_42 (and_42_out, A[1], B[5]);
  somador_1bit somador_1bit_38 (
    .a(somador_1bit_37_s), .b(and_42_out), .Cin(meio_somador_4_cout), .S(somador_1bit_38_s),
    .Cout(somador_1bit_38_cout));
  and and_43 (and_43_out, A[0], B[6]);
  meio_somador meio_somador_3 (.a(somador_1bit_38_s), .b(and_43_out), .s(saida[6]), .cout(meio_somador_3_cout));
  and and_44 (and_44_out, A[5], B[0]);
  and and_45 (and_45_out, A[4], B[1]);
  somador_1bit somador_1bit_39 (
    .a(and_44_out), .b(and_45_out), .Cin(somador_1bit_43_cout), .S(somador_1bit_39_s),
    .Cout(somador_1bit_39_cout));
  and and_46 (and_46_out, A[3], B[2]);
  somador_1bit somador_1bit_40 (
    .a(somador_1bit_39_s), .b(and_46_out), .Cin(somador_1bit_44_cout), .S(somador_1bit_40_s),
    .Cout(somador_1bit_40_cout));
  and and_47 (and_47_out, A[2], B[3]);
  somador_1bit somador_1bit_41 (
    .a(somador_1bit_40_s), .b(and_47_out), .Cin(somador_1bit_45_cout), .S(somador_1bit_41_s),
    .Cout(somador_1bit_41_cout));
  and and_48 (and_48_out, A[1], B[4]);
  somador_1bit somador_1bit_42 (
    .a(somador_1bit_41_s), .b(and_48_out), .Cin(meio_somador_5_cout), .S(somador_1bit_42_s),
    .Cout(somador_1bit_42_cout));
  and and_49 (and_49_out, A[0], B[5]);
  meio_somador meio_somador_4 (.a(somador_1bit_42_s), .b(and_49_out), .s(saida[5]), .cout(meio_somador_4_cout));
  and and_50 (and_50_out, A[4], B[0]);
  and and_51 (and_51_out, A[3], B[1]);
  somador_1bit somador_1bit_43 (
    .a(and_51_out), .b(and_50_out), .Cin(somador_1bit_47_cout), .S(somador_1bit_43_s),
    .Cout(somador_1bit_43_cout));
  and and_52 (and_52_out, A[2], B[2]);
  somador_1bit somador_1bit_44 (
    .a(somador_1bit_43_s), .b(and_52_out), .Cin(somador_1bit_46_cout), .S(somador_1bit_44_s),
    .Cout(somador_1bit_44_cout));
  and and_53 (and_53_out, A[1], B[3]);
  somador_1bit somador_1bit_45 (
    .a(somador_1bit_44_s), .b(and_53_out), .Cin(meio_somador_6_cout), .S(somador_1bit_45_s),
    .Cout(somador_1bit_45_cout));
  and and_54 (and_54_out, A[0], B[4]);
  meio_somador meio_somador_5 (.a(somador_1bit_45_s), .b(and_54_out), .s(saida[4]), .cout(meio_somador_5_cout));
  and and_55 (and_55_out, A[3], B[0]);
  and and_56 (and_56_out, A[2], B[1]);
  and and_57 (and_57_out, A[1], B[2]);
  somador_1bit somador_1bit_46 (
    .a(somador_1bit_47_s), .b(and_57_out), .Cin(meio_somador_7_cout), .S(somador_1bit_46_s),
    .Cout(somador_1bit_46_cout));
  and and_58 (and_58_out, A[0], B[3]);
  meio_somador meio_somador_6 (.a(somador_1bit_46_s), .b(and_58_out), .s(saida[3]), .cout(meio_somador_6_cout));
  and and_59 (and_59_out, A[2], B[0]);
  and and_60 (and_60_out, A[1], B[1]);
  somador_1bit somador_1bit_47 (
    .a(and_55_out), .b(and_56_out), .Cin(somador_1bit_48_cout), .S(somador_1bit_47_s),
    .Cout(somador_1bit_47_cout));
  and and_61 (and_61_out, A[0], B[2]);
  and and_62 (and_62_out, A[1], B[0]);
  and and_63 (and_63_out, A[0], B[1]);
  somador_1bit somador_1bit_48 (
    .a(and_59_out), .b(and_60_out), .Cin(meio_somador_8_cout), .S(somador_1bit_48_s),
    .Cout(somador_1bit_48_cout));
  meio_somador meio_somador_7 (.a(somador_1bit_48_s), .b(and_61_out), .s(saida[2]), .cout(meio_somador_7_cout));
  meio_somador meio_somador_8 (.a(and_62_out), .b(and_63_out), .s(saida[1]), .cout(meio_somador_8_cout));
  and and_64 (saida[0], A[0], B[0]);
endmodule

module somador_1bit (
  input  a,
  input  b,
  input  Cin,
  output S,
  output Cout
);

  wire and_1_out, and_2_out, and_3_out, and_4_out, and_5_out, and_6_out, and_7_out, not_1_out, not_2_out,
       not_3_out, not_4_out, not_5_out, not_6_out;

  not not_1 (not_1_out, a);
  not not_2 (not_2_out, b);
  not not_3 (not_3_out, a);
  not not_4 (not_4_out, Cin);
  not not_5 (not_5_out, b);
  not not_6 (not_6_out, Cin);
  and and_1 (and_1_out, b, Cin);
  and and_2 (and_2_out, a, Cin);
  and and_3 (and_3_out, a, b);
  and and_4 (and_4_out, not_1_out, not_2_out, Cin);
  and and_5 (and_5_out, not_3_out, b, not_4_out);
  and and_6 (and_6_out, a, not_5_out, not_6_out);
  and and_7 (and_7_out, a, b, Cin);
  or or_1 (Cout, and_1_out, and_2_out, and_3_out);
  or or_2 (S, and_4_out, and_5_out, and_6_out, and_7_out);
endmodule

module meio_somador (
  input  a,
  input  b,
  output s,
  output cout
);

  wire and_2_out, and_3_out, not_1_out, not_2_out;

  not not_1 (not_1_out, a);
  not not_2 (not_2_out, b);
  and and_1 (cout, a, b);
  and and_2 (and_2_out, not_1_out, b);
  and and_3 (and_3_out, a, not_2_out);
  or or_1 (s, and_2_out, and_3_out);
endmodule
