// Logisim project clock.circ as structural Verilog: 3 circuits, main circuit main
module main (
  input  clock,
  output Hora,
  output [3:0] out_3,
  output [3:0] out_4
);

  wire and_1_out, and_2_out;

  and and_1 (and_1_out, out_4[3], ~out_4[2], out_4[1], ~out_4[0]);  // AND_Gate
  and and_2 (and_2_out, ~out_3[3], Hora, out_3[1], ~out_3[0]);  // AND_Gate
  J_K_Flip_Flop #(.trigger("falling")) j_k_ff_1 (
    .J(1'b1), .clk(out_4[3]), .K(1'b1), .Q(out_3[0]), .reset(and_2_out));  // open: Qn, preset, en
  J_K_Flip_Flop #(.trigger("falling")) j_k_ff_2 (
    .J(1'b1), .clk(clock), .K(1'b1), .Q(out_4[0]), .reset(and_1_out));  // open: Qn, preset, en
  J_K_Flip_Flop #(.trigger("falling")) j_k_ff_3 (
    .J(1'b1), .clk(out_4[0]), .K(1'b1), .Q(out_4[1]), .reset(and_1_out));  // open: Qn, preset, en
  J_K_Flip_Flop #(.trigger("falling")) j_k_ff_4 (
    .J(1'b1), .clk(out_3[0]), .K(1'b1), .Q(out_3[1]), .reset(and_2_out));  // open: Qn, preset, en
  J_K_Flip_Flop #(.trigger("falling")) j_k_ff_5 (
    .J(1'b1), .clk(out_3[1]), .K(1'b1), .Q(Hora), .reset(and_2_out));  // open: Qn, preset, en
  J_K_Flip_Flop #(.trigger("falling")) j_k_ff_6 (
    .J(1'b1), .clk(out_4[1]), .K(1'b1), .Q(out_4[2]), .reset(and_1_out));  // open: Qn, preset, en
  J_K_Flip_Flop #(.trigger("falling")) j_k_ff_7 (
    .J(1'b1), .clk(out_4[2]), .K(1'b1), .Q(out_4[3]), .reset(and_1_out));  // open: Qn, preset, en
  J_K_Flip_Flop #(.trigger("falling")) j_k_ff_8 (
    .J(1'b1), .clk(Hora), .K(1'b1), .Q(out_3[3]), .reset(and_2_out));  // open: Qn, preset, en

  assign out_3[2] = Hora;
endmodule

module RELOGIO (
);

  wire clock_1_out, main_1_hora, main_2_hora;
  wire [3:0] horas_1_out_3, horas_1_out_4, main_1_out_3, main_1_out_4, main_2_out_3, main_2_out_4;

  Hex_Digit_Display hex_digit_display_1 (.value(horas_1_out_3));  // open: dp
  Hex_Digit_Display hex_digit_display_2 (.value(horas_1_out_4));  // open: dp
  horas horas_1 (.out_4(horas_1_out_4), .Clock(main_1_hora), .out_3(horas_1_out_3));  // open: clock_out
  Hex_Digit_Display hex_digit_display_3 (.value(main_1_out_3));  // open: dp
  Hex_Digit_Display hex_digit_display_4 (.value(main_1_out_4));  // open: dp
  main main_1 (.out_4(main_1_out_4), .clock(main_2_hora), .out_3(main_1_out_3), .Hora(main_1_hora));
  Hex_Digit_Display hex_digit_display_5 (.value(main_2_out_3));  // open: dp
  Hex_Digit_Display hex_digit_display_6 (.value(main_2_out_4));  // open: dp
  Clock clock_1 (.out(clock_1_out));
  main main_2 (.out_4(main_2_out_4), .clock(clock_1_out), .out_3(main_2_out_3), .Hora(main_2_hora));
endmodule

module horas (
  input  Clock,
  output clock_out,
  output [3:0] out_3,
  output [3:0] out_4
);

  wire and_1_out, and_2_out, and_3_out, or_1_out, or_2_out;

  and and_1 (and_1_out, out_4[2], ~out_3[0], clock_out, ~out_3[2], ~out_3[3]);  // AND_Gate
  or or_1 (or_1_out, and_1_out, and_2_out);
  and and_2 (and_2_out, ~out_3[3], ~out_3[2], clock_out, out_3[0]);  // AND_Gate
  and and_3 (and_3_out, out_4[3], ~out_4[2], out_4[1], ~out_4[0]);  // AND_Gate
  or or_2 (or_2_out, and_1_out, and_3_out);
  J_K_Flip_Flop #(.trigger("falling")) j_k_ff_1 (
    .J(1'b1), .clk(Clock), .K(1'b1), .Q(out_4[0]), .reset(or_2_out));  // open: Qn, preset, en
  J_K_Flip_Flop #(.trigger("falling")) j_k_ff_2 (
    .J(1'b1), .clk(out_4[3]), .K(1'b1), .Q(out_3[0]), .reset(or_1_out));  // open: Qn, preset, en
  J_K_Flip_Flop #(.trigger("falling")) j_k_ff_3 (
    .J(1'b1), .clk(out_3[0]), .K(1'b1), .Q(clock_out), .reset(or_1_out));  // open: Qn, preset, en
  J_K_Flip_Flop #(.trigger("falling")) j_k_ff_4 (
    .J(1'b1), .clk(out_4[0]), .K(1'b1), .Q(out_4[1]), .reset(or_2_out));  // open: Qn, preset, en
  J_K_Flip_Flop #(.trigger("falling")) j_k_ff_5 (
    .J(1'b1), .clk(out_4[1]), .K(1'b1), .Q(out_4[2]), .reset(or_2_out));  // open: Qn, preset, en
  J_K_Flip_Flop #(.trigger("falling")) j_k_ff_6 (
    .J(1'b1), .clk(clock_out), .K(1'b1), .Q(out_3[2]), .reset(or_1_out));  // open: Qn, preset, en
  J_K_Flip_Flop #(.trigger("falling")) j_k_ff_7 (
    .J(1'b1), .clk(out_3[2]), .K(1'b1), .Q(out_3[3]), .reset(or_1_out));  // open: Qn, preset, en
  J_K_Flip_Flop #(.trigger("falling")) j_k_ff_8 (
    .J(1'b1), .clk(out_4[2]), .K(1'b1), .Q(out_4[3]), .reset(or_2_out));  // open: Qn, preset, en
  Hex_Digit_Display hex_digit_display_1 (.value({out_3[3:2], clock_out, out_3[0]}));  // open: dp
  Hex_Digit_Display hex_digit_display_2 (.value(out_4));  // open: dp

  assign out_3[1] = clock_out;
endmodule
