// Logisim project ula.circ as structural Verilog: 8 circuits, main circuit main
module main (
  input  [10:0] entrada,
  input  escrever,
  output [10:0] Dado,
  output [2:0] out_4,
  output [7:0] resto_divisao,
  output [15:0] Resultado_multiplicacao,
  output [7:0] out_7
);

  wire clock_1_out;
  wire [7:0] ula_1_saida;

  Clock clock_1 (.out(clock_1_out));
  contador contador_1 (.entrada(clock_1_out), .saida(out_4));
  selecao selecao_1 (.selecao(out_4), .ler_escrever(escrever), .entrada(entrada), .saida(Dado));
  ula ula_1 (
    .a(Dado[7:0]), .b(out_7), .operacao(Dado[10:8]), .saida(ula_1_saida), .Resto_divisao(resto_divisao),
    .Resultado_multiplicacao(Resultado_multiplicacao));
  acumulador acumulador_1 (.saida(out_7), .entrada(ula_1_saida), .ler_escrever(clock_1_out));
endmodule

module memoria_11_bits (
  input  [2:0] selecao,
  input  [10:0] entrada,
  input  ler_escrever,
  output [10:0] saida
);

  wire and_1_out, and_2_out, and_3_out, and_4_out, and_5_out, and_6_out, and_7_out, and_8_out, and_9_out,
       and_10_out, and_11_out, and_12_out, and_13_out, and_14_out, and_15_out, and_16_out, and_17_out,
       and_18_out, and_19_out, and_20_out, and_21_out, and_22_out, and_23_out, and_24_out, and_25_out,
       and_26_out, and_27_out, and_28_out, and_29_out, and_30_out, and_31_out, and_32_out, and_33_out,
       and_34_out, and_35_out, and_36_out, and_37_out, and_38_out, and_39_out, and_40_out, and_41_out,
       and_42_out, and_43_out, and_44_out, and_45_out, and_46_out, and_47_out, and_48_out, and_49_out,
       and_50_out, and_51_out, and_52_out, and_53_out, and_54_out, and_55_out, and_56_out, and_57_out,
       and_58_out, and_59_out, and_60_out, and_61_out, and_62_out, and_63_out, and_64_out, and_65_out,
       and_66_out, and_67_out, and_68_out, and_69_out, and_70_out, and_71_out, and_72_out, and_73_out,
       and_74_out, and_75_out, and_76_out, and_77_out, and_78_out, and_79_out, and_80_out, and_81_out,
       and_82_out, and_83_out, and_84_out, and_85_out, and_86_out, and_87_out, and_88_out, and_89_out,
       and_90_out, and_91_out, and_92_out, and_93_out, and_94_out, and_95_out, and_96_out, and_97_out,
       and_98_out, and_99_out, and_100_out, and_101_out, and_102_out, and_103_out, and_104_out, d_ff_1_q,
       d_ff_2_q, d_ff_3_q, d_ff_4_q, d_ff_5_q, d_ff_6_q, d_ff_7_q, d_ff_8_q, d_ff_9_q, d_ff_10_q, d_ff_11_q,
       d_ff_12_q, d_ff_13_q, d_ff_14_q, d_ff_15_q, d_ff_16_q, d_ff_17_q, d_ff_18_q, d_ff_19_q, d_ff_20_q,
       d_ff_21_q, d_ff_22_q, d_ff_23_q, d_ff_24_q, d_ff_25_q, d_ff_26_q, d_ff_27_q, d_ff_28_q, d_ff_29_q,
       d_ff_30_q, d_ff_31_q, d_ff_32_q, d_ff_33_q, d_ff_34_q, d_ff_35_q, d_ff_36_q, d_ff_37_q, d_ff_38_q,
       d_ff_39_q, d_ff_40_q, d_ff_41_q, d_ff_42_q, d_ff_43_q, d_ff_44_q, d_ff_45_q, d_ff_46_q, d_ff_47_q,
       d_ff_48_q, d_ff_49_q, d_ff_50_q, d_ff_51_q, d_ff_52_q, d_ff_53_q, d_ff_54_q, d_ff_55_q, d_ff_56_q,
       d_ff_57_q, d_ff_58_q, d_ff_59_q, d_ff_60_q, d_ff_61_q, d_ff_62_q, d_ff_63_q, d_ff_64_q, d_ff_65_q,
       d_ff_66_q, d_ff_67_q, d_ff_68_q, d_ff_69_q, d_ff_70_q, d_ff_71_q, d_ff_72_q, d_ff_73_q, d_ff_74_q,
       d_ff_75_q, d_ff_76_q, d_ff_77_q, d_ff_78_q, d_ff_79_q, d_ff_80_q, d_ff_81_q, d_ff_82_q, d_ff_83_q,
       d_ff_84_q, d_ff_85_q, d_ff_86_q, d_ff_87_q, d_ff_88_q;

  and and_1 (and_1_out, ~selecao[2], ~selecao[1], ~selecao[0]);  // AND_Gate
  and and_2 (and_2_out, ~selecao[2], ~selecao[1], selecao[0]);  // AND_Gate
  and and_3 (and_3_out, ~selecao[2], selecao[1], ~selecao[0]);  // AND_Gate
  and and_4 (and_4_out, ~selecao[2], selecao[1], selecao[0]);  // AND_Gate
  and and_5 (and_5_out, selecao[2], ~selecao[1], ~selecao[0]);  // AND_Gate
  and and_6 (and_6_out, selecao[2], ~selecao[1], selecao[0]);  // AND_Gate
  and and_7 (and_7_out, selecao[2], selecao[1], ~selecao[0]);  // AND_Gate
  and and_8 (and_8_out, selecao[2], selecao[1], selecao[0]);
  and and_9 (and_9_out, and_1_out, ler_escrever);
  and and_10 (and_10_out, and_2_out, ler_escrever);
  and and_11 (and_11_out, and_3_out, ler_escrever);
  and and_12 (and_12_out, and_4_out, ler_escrever);
  and and_13 (and_13_out, and_5_out, ler_escrever);
  and and_14 (and_14_out, and_6_out, ler_escrever);
  and and_15 (and_15_out, and_7_out, ler_escrever);
  and and_16 (and_16_out, and_8_out, ler_escrever);
  D_Flip_Flop d_ff_1 (.clk(and_9_out), .D(entrada[10]), .Q(d_ff_1_q));  // open: Qn, preset, en, reset
  and and_17 (and_17_out, d_ff_1_q, and_1_out);
  D_Flip_Flop d_ff_2 (.clk(and_10_out), .D(entrada[10]), .Q(d_ff_2_q));  // open: Qn, preset, en, reset
  D_Flip_Flop d_ff_3 (.clk(and_11_out), .D(entrada[10]), .Q(d_ff_3_q));  // open: Qn, preset, en, reset
  D_Flip_Flop d_ff_4 (.clk(and_12_out), .D(entrada[10]), .Q(d_ff_4_q));  // open: Qn, preset, en, reset
  D_Flip_Flop d_ff_5 (.clk(and_13_out), .D(entrada[10]), .Q(d_ff_5_q));  // open: Qn, preset, en, reset
  D_Flip_Flop d_ff_6 (.clk(and_14_out), .D(entrada[10]), .Q(d_ff_6_q));  // open: Qn, preset, en, reset
  D_Flip_Flop d_ff_7 (.clk(and_15_out), .D(entrada[10]), .Q(d_ff_7_q));  // open: Qn, preset, en, reset
  D_Flip_Flop d_ff_8 (.clk(and_16_out), .D(entrada[10]), .Q(d_ff_8_q));  // open: Qn, preset, en, reset
  and and_18 (and_18_out, d_ff_2_q, and_2_out);
  and and_19 (and_19_out, d_ff_3_q, and_3_out);
  and and_20 (and_20_out, d_ff_4_q, and_4_out);
  and and_21 (and_21_out, d_ff_5_q, and_5_out);
  or or_1 (saida[10], and_17_out, and_18_out, and_19_out, and_20_out, and_21_out, and_22_out, and_23_out, and_24_out);
  and and_22 (and_22_out, d_ff_6_q, and_6_out);
  and and_23 (and_23_out, d_ff_7_q, and_7_out);
  and and_24 (and_24_out, d_ff_8_q, and_8_out);
  D_Flip_Flop d_ff_9 (.clk(and_9_out), .D(entrada[9]), .Q(d_ff_9_q));  // open: Qn, preset, en, reset
  and and_25 (and_25_out, d_ff_9_q, and_1_out);
  D_Flip_Flop d_ff_10 (.clk(and_10_out), .D(entrada[9]), .Q(d_ff_10_q));  // open: Qn, preset, en, reset
  D_Flip_Flop d_ff_11 (.clk(and_11_out), .D(entrada[9]), .Q(d_ff_11_q));  // open: Qn, preset, en, reset
  D_Flip_Flop d_ff_12 (.clk(and_12_out), .D(entrada[9]), .Q(d_ff_12_q));  // open: Qn, preset, en, reset
  D_Flip_Flop d_ff_13 (.clk(and_13_out), .D(entrada[9]), .Q(d_ff_13_q));  // open: Qn, preset, en, reset
  D_Flip_Flop d_ff_14 (.clk(and_14_out), .D(entrada[9]), .Q(d_ff_14_q));  // open: Qn, preset, en, reset
  D_Flip_Flop d_ff_15 (.clk(and_15_out), .D(entrada[9]), .Q(d_ff_15_q));  // open: Qn, preset, en, reset
  D_Flip_Flop d_ff_16 (.clk(and_16_out), .D(entrada[9]), .Q(d_ff_16_q));  // open: Qn, preset, en, reset
  and and_26 (and_26_out, d_ff_10_q, and_2_out);
  and and_27 (and_27_out, d_ff_11_q, and_3_out);
  and and_28 (and_28_out, d_ff_12_q, and_4_out);
  and and_29 (and_29_out, d_ff_13_q, and_5_out);
  or or_2 (saida[9], and_25_out, and_26_out, and_27_out, and_28_out, and_29_out, and_30_out, and_31_out, and_32_out);
  and and_30 (and_30_out, d_ff_14_q, and_6_out);
  and and_31 (and_31_out, d_ff_15_q, and_7_out);
  and and_32 (and_32_out, d_ff_16_q, and_8_out);
  D_Flip_Flop d_ff_17 (.clk(and_14_out), .D(entrada[8]), .Q(d_ff_17_q));  // open: Qn, preset, en, reset
  D_Flip_Flop d_ff_18 (.clk(and_15_out), .D(entrada[8]), .Q(d_ff_18_q));  // open: Qn, preset, en, reset
  D_Flip_Flop d_ff_19 (.clk(and_16_out), .D(entrada[8]), .Q(d_ff_19_q));  // open: Qn, preset, en, reset
  D_Flip_Flop d_ff_20 (.clk(and_9_out), .D(entrada[8]), .Q(d_ff_20_q));  // open: Qn, preset, en, reset
  and and_33 (and_33_out, d_ff_20_q, and_1_out);
  D_Flip_Flop d_ff_21 (.clk(and_10_out), .D(entrada[8]), .Q(d_ff_21_q));  // open: Qn, preset, en, reset
  D_Flip_Flop d_ff_22 (.clk(and_11_out), .D(entrada[8]), .Q(d_ff_22_q));  // open: Qn, preset, en, reset
  D_Flip_Flop d_ff_23 (.clk(and_12_out), .D(entrada[8]), .Q(d_ff_23_q));  // open: Qn, preset, en, reset
  D_Flip_Flop d_ff_24 (.clk(and_13_out), .D(entrada[8]), .Q(d_ff_24_q));  // open: Qn, preset, en, reset
  and and_34 (and_34_out, d_ff_21_q, and_2_out);
  and and_35 (and_35_out, d_ff_22_q, and_3_out);
  and and_36 (and_36_out, d_ff_23_q, and_4_out);
  or or_3 (saida[8], and_33_out, and_34_out, and_35_out, and_36_out, and_37_out, and_38_out, and_39_out, and_40_out);
  and and_37 (and_37_out, d_ff_24_q, and_5_out);
  and and_38 (and_38_out, d_ff_17_q, and_6_out);
  and and_39 (and_39_out, d_ff_18_q, and_7_out);
  and and_40 (and_40_out, d_ff_19_q, and_8_out);
  D_Flip_Flop d_ff_25 (.clk(and_9_out), .D(entrada[7]), .Q(d_ff_25_q));  // open: Qn, preset, en, reset
  and and_41 (and_41_out, d_ff_25_q, and_1_out);
  D_Flip_Flop d_ff_26 (.clk(and_10_out), .D(entrada[7]), .Q(d_ff_26_q));  // open: Qn, preset, en, reset
  D_Flip_Flop d_ff_27 (.clk(and_11_out), .D(entrada[7]), .Q(d_ff_27_q));  // open: Qn, preset, en, reset
  D_Flip_Flop d_ff_28 (.clk(and_12_out), .D(entrada[7]), .Q(d_ff_28_q));  // open: Qn, preset, en, reset
  D_Flip_Flop d_ff_29 (.clk(and_13_out), .D(entrada[7]), .Q(d_ff_29_q));  // open: Qn, preset, en, reset
  D_Flip_Flop d_ff_30 (.clk(and_14_out), .D(entrada[7]), .Q(d_ff_30_q));  // open: Qn, preset, en, reset
  D_Flip_Flop d_ff_31 (.clk(and_15_out), .D(entrada[7]), .Q(d_ff_31_q));  // open: Qn, preset, en, reset
  D_Flip_Flop d_ff_32 (.clk(and_16_out), .D(entrada[7]), .Q(d_ff_32_q));  // open: Qn, preset, en, reset
  and and_42 (and_42_out, d_ff_26_q, and_2_out);
  and and_43 (and_43_out, d_ff_27_q, and_3_out);
  and and_44 (and_44_out, d_ff_28_q, and_4_out);
  and and_45 (and_45_out, d_ff_29_q, and_5_out);
  or or_4 (saida[7], and_41_out, and_42_out, and_43_out, and_44_out, and_45_out, and_46_out, and_47_out, and_48_out);
  and and_46 (and_46_out, d_ff_30_q, and_6_out);
  and and_47 (and_47_out, d_ff_31_q, and_7_out);
  and and_48 (and_48_out, d_ff_32_q, and_8_out);
  D_Flip_Flop d_ff_33 (.clk(and_9_out), .D(entrada[6]), .Q(d_ff_33_q));  // open: Qn, preset, en, reset
  D_Flip_Flop d_ff_34 (.clk(and_10_out), .D(entrada[6]), .Q(d_ff_34_q));  // open: Qn, preset, en, reset
  D_Flip_Flop d_ff_35 (.clk(and_11_out), .D(entrada[6]), .Q(d_ff_35_q));  // open: Qn, preset, en, reset
  D_Flip_Flop d_ff_36 (.clk(and_12_out), .D(entrada[6]), .Q(d_ff_36_q));  // open: Qn, preset, en, reset
  D_Flip_Flop d_ff_37 (.clk(and_13_out), .D(entrada[6]), .Q(d_ff_37_q));  // open: Qn, preset, en, reset
  D_Flip_Flop d_ff_38 (.clk(and_14_out), .D(entrada[6]), .Q(d_ff_38_q));  // open: Qn, preset, en, reset
  D_Flip_Flop d_ff_39 (.clk(and_15_out), .D(entrada[6]), .Q(d_ff_39_q));  // open: Qn, preset, en, reset
  D_Flip_Flop d_ff_40 (.clk(and_16_out), .D(entrada[6]), .Q(d_ff_40_q));  // open: Qn, preset, en, reset
  and and_49 (and_49_out, d_ff_33_q, and_1_out);
  and and_50 (and_50_out, d_ff_34_q, and_2_out);
  and and_51 (and_51_out, d_ff_35_q, and_3_out);
  and and_52 (and_52_out, d_ff_36_q, and_4_out);
  or or_5 (saida[6], and_49_out, and_50_out, and_51_out, and_52_out, and_53_out, and_54_out, and_55_out, and_56_out);
  and and_53 (and_53_out, d_ff_37_q, and_5_out);
  and and_54 (and_54_out, d_ff_38_q, and_6_out);
  and and_55 (and_55_out, d_ff_39_q, and_7_out);
  and and_56 (and_56_out, d_ff_40_q, and_8_out);
  D_Flip_Flop d_ff_41 (.clk(and_14_out), .D(entrada[5]), .Q(d_ff_41_q));  // open: Qn, preset, en, reset
  D_Flip_Flop d_ff_42 (.clk(and_15_out), .D(entrada[5]), .Q(d_ff_42_q));  // open: Qn, preset, en, reset
  D_Flip_Flop d_ff_43 (.clk(and_16_out), .D(entrada[5]), .Q(d_ff_43_q));  // open: Qn, preset, en, reset
  D_Flip_Flop d_ff_44 (.clk(and_9_out), .D(entrada[5]), .Q(d_ff_44_q));  // open: Qn, preset, en, reset
  and and_57 (and_57_out, d_ff_44_q, and_1_out);
  D_Flip_Flop d_ff_45 (.clk(and_10_out), .D(entrada[5]), .Q(d_ff_45_q));  // open: Qn, preset, en, reset
  D_Flip_Flop d_ff_46 (.clk(and_11_out), .D(entrada[5]), .Q(d_ff_46_q));  // open: Qn, preset, en, reset
  D_Flip_Flop d_ff_47 (.clk(and_12_out), .D(entrada[5]), .Q(d_ff_47_q));  // open: Qn, preset, en, reset
  D_Flip_Flop d_ff_48 (.clk(and_13_out), .D(entrada[5]), .Q(d_ff_48_q));  // open: Qn, preset, en, reset
  and and_58 (and_58_out, d_ff_45_q, and_2_out);
  and and_59 (and_59_out, d_ff_46_q, and_3_out);
  and and_60 (and_60_out, d_ff_47_q, and_4_out);
  or or_6 (saida[5], and_57_out, and_58_out, and_59_out, and_60_out, and_61_out, and_62_out, and_63_out, and_64_out);
  and and_61 (and_61_out, d_ff_48_q, and_5_out);
  and and_62 (and_62_out, d_ff_41_q, and_6_out);
  and and_63 (and_63_out, d_ff_42_q, and_7_out);
  and and_64 (and_64_out, d_ff_43_q, and_8_out);
  D_Flip_Flop d_ff_49 (.clk(and_9_out), .D(entrada[4]), .Q(d_ff_49_q));  // open: Qn, preset, en, reset
  D_Flip_Flop d_ff_50 (.clk(and_10_out), .D(entrada[4]), .Q(d_ff_50_q));  // open: Qn, preset, en, reset
  D_Flip_Flop d_ff_51 (.clk(and_11_out), .D(entrada[4]), .Q(d_ff_51_q));  // open: Qn, preset, en, reset
  D_Flip_Flop d_ff_52 (.clk(and_12_out), .D(entrada[4]), .Q(d_ff_52_q));  // open: Qn, preset, en, reset
  D_Flip_Flop d_ff_53 (.clk(and_13_out), .D(entrada[4]), .Q(d_ff_53_q));  // open: Qn, preset, en, reset
  D_Flip_Flop d_ff_54 (.clk(and_14_out), .D(entrada[4]), .Q(d_ff_54_q));  // open: Qn, preset, en, reset
  D_Flip_Flop d_ff_55 (.clk(and_15_out), .D(entrada[4]), .Q(d_ff_55_q));  // open: Qn, preset, en, reset
  D_Flip_Flop d_ff_56 (.clk(and_16_out), .D(entrada[4]), .Q(d_ff_56_q));  // open: Qn, preset, en, reset
  and and_65 (and_65_out, d_ff_49_q, and_1_out);
  and and_66 (and_66_out, d_ff_50_q, and_2_out);
  and and_67 (and_67_out, d_ff_51_q, and_3_out);
  and and_68 (and_68_out, d_ff_52_q, and_4_out);
  and and_69 (and_69_out, d_ff_53_q, and_5_out);
  or or_7 (saida[4], and_65_out, and_66_out, and_67_out, and_68_out, and_69_out, and_70_out, and_71_out, and_72_out);
  and and_70 (and_70_out, d_ff_54_q, and_6_out);
  and and_71 (and_71_out, d_ff_55_q, and_7_out);
  and and_72 (and_72_out, d_ff_56_q, and_8_out);
  D_Flip_Flop d_ff_57 (.clk(and_9_out), .D(entrada[3]), .Q(d_ff_57_q));  // open: Qn, preset, en, reset
  D_Flip_Flop d_ff_58 (.clk(and_10_out), .D(entrada[3]), .Q(d_ff_58_q));  // open: Qn, preset, en, reset
  D_Flip_Flop d_ff_59 (.clk(and_11_out), .D(entrada[3]), .Q(d_ff_59_q));  // open: Qn, preset, en, reset
  D_Flip_Flop d_ff_60 (.clk(and_12_out), .D(entrada[3]), .Q(d_ff_60_q));  // open: Qn, preset, en, reset
  D_Flip_Flop d_ff_61 (.clk(and_13_out), .D(entrada[3]), .Q(d_ff_61_q));  // open: Qn, preset, en, reset
  D_Flip_Flop d_ff_62 (.clk(and_14_out), .D(entrada[3]), .Q(d_ff_62_q));  // open: Qn, preset, en, reset
  D_Flip_Flop d_ff_63 (.clk(and_15_out), .D(entrada[3]), .Q(d_ff_63_q));  // open: Qn, preset, en, reset
  D_Flip_Flop d_ff_64 (.clk(and_16_out), .D(entrada[3]), .Q(d_ff_64_q));  // open: Qn, preset, en, reset
  and and_73 (and_73_out, d_ff_57_q, and_1_out);
  and and_74 (and_74_out, d_ff_58_q, and_2_out);
  and and_75 (and_75_out, d_ff_59_q, and_3_out);
  and and_76 (and_76_out, d_ff_60_q, and_4_out);
  or or_8 (saida[3], and_73_out, and_74_out, and_75_out, and_76_out, and_77_out, and_78_out, and_79_out, and_80_out);
  and and_77 (and_77_out, d_ff_61_q, and_5_out);
  and and_78 (and_78_out, d_ff_62_q, and_6_out);
  and and_79 (and_79_out, d_ff_63_q, and_7_out);
  and and_80 (and_80_out, d_ff_64_q, and_8_out);
  D_Flip_Flop d_ff_65 (.clk(and_9_out), .D(entrada[2]), .Q(d_ff_65_q));  // open: Qn, preset, en, reset
  D_Flip_Flop d_ff_66 (.clk(and_10_out), .D(entrada[2]), .Q(d_ff_66_q));  // open: Qn, preset, en, reset
  D_Flip_Flop d_ff_67 (.clk(and_11_out), .D(entrada[2]), .Q(d_ff_67_q));  // open: Qn, preset, en, reset
  D_Flip_Flop d_ff_68 (.clk(and_12_out), .D(entrada[2]), .Q(d_ff_68_q));  // open: Qn, preset, en, reset
  D_Flip_Flop d_ff_69 (.clk(and_13_out), .D(entrada[2]), .Q(d_ff_69_q));  // open: Qn, preset, en, reset
  D_Flip_Flop d_ff_70 (.clk(and_14_out), .D(entrada[2]), .Q(d_ff_70_q));  // open: Qn, preset, en, reset
  D_Flip_Flop d_ff_71 (.clk(and_15_out), .D(entrada[2]), .Q(d_ff_71_q));  // open: Qn, preset, en, reset
  D_Flip_Flop d_ff_72 (.clk(and_16_out), .D(entrada[2]), .Q(d_ff_72_q));  // open: Qn, preset, en, reset
  and and_81 (and_81_out, d_ff_65_q, and_1_out);
  and and_82 (and_82_out, d_ff_66_q, and_2_out);
  and and_83 (and_83_out, d_ff_67_q, and_3_out);
  and and_84 (and_84_out, d_ff_68_q, and_4_out);
  and and_85 (and_85_out, d_ff_69_q, and_5_out);
  or or_9 (saida[2], and_81_out, and_82_out, and_83_out, and_84_out, and_85_out, and_86_out, and_87_out, and_88_out);
  and and_86 (and_86_out, d_ff_70_q, and_6_out);
  and and_87 (and_87_out, d_ff_71_q, and_7_out);
  and and_88 (and_88_out, d_ff_72_q, and_8_out);
  D_Flip_Flop d_ff_73 (.clk(and_9_out), .D(entrada[1]), .Q(d_ff_73_q));  // open: Qn, preset, en, reset
  and and_89 (and_89_out, d_ff_73_q, and_1_out);
  D_Flip_Flop d_ff_74 (.clk(and_10_out), .D(entrada[1]), .Q(d_ff_74_q));  // open: Qn, preset, en, reset
  D_Flip_Flop d_ff_75 (.clk(and_11_out), .D(entrada[1]), .Q(d_ff_75_q));  // open: Qn, preset, en, reset
  D_Flip_Flop d_ff_76 (.clk(and_12_out), .D(entrada[1]), .Q(d_ff_76_q));  // open: Qn, preset, en, reset
  D_Flip_Flop d_ff_77 (.clk(and_13_out), .D(entrada[1]), .Q(d_ff_77_q));  // open: Qn, preset, en, reset
  D_Flip_Flop d_ff_78 (.clk(and_14_out), .D(entrada[1]), .Q(d_ff_78_q));  // open: Qn, preset, en, reset
  D_Flip_Flop d_ff_79 (.clk(and_15_out), .D(entrada[1]), .Q(d_ff_79_q));  // open: Qn, preset, en, reset
  D_Flip_Flop d_ff_80 (.clk(and_16_out), .D(entrada[1]), .Q(d_ff_80_q));  // open: Qn, preset, en, reset
  and and_90 (and_90_out, d_ff_74_q, and_2_out);
  and and_91 (and_91_out, d_ff_75_q, and_3_out);
  and and_92 (and_92_out, d_ff_76_q, and_4_out);
  and and_93 (and_93_out, d_ff_77_q, and_5_out);
  or or_10 (saida[1], and_89_out, and_90_out, and_91_out, and_92_out, and_93_out, and_94_out, and_95_out, and_96_out);
  and and_94 (and_94_out, d_ff_78_q, and_6_out);
  and and_95 (and_95_out, d_ff_79_q, and_7_out);
  and and_96 (and_96_out, d_ff_80_q, and_8_out);
  D_Flip_Flop d_ff_81 (.clk(and_9_out), .D(entrada[0]), .Q(d_ff_81_q));  // open: Qn, preset, en, reset
  and and_97 (and_97_out, d_ff_81_q, and_1_out);
  D_Flip_Flop d_ff_82 (.clk(and_10_out), .D(entrada[0]), .Q(d_ff_82_q));  // open: Qn, preset, en, reset
  D_Flip_Flop d_ff_83 (.clk(and_11_out), .D(entrada[0]), .Q(d_ff_83_q));  // open: Qn, preset, en, reset
  D_Flip_Flop d_ff_84 (.clk(and_12_out), .D(entrada[0]), .Q(d_ff_84_q));  // open: Qn, preset, en, reset
  D_Flip_Flop d_ff_85 (.clk(and_13_out), .D(entrada[0]), .Q(d_ff_85_q));  // open: Qn, preset, en, reset
  D_Flip_Flop d_ff_86 (.clk(and_14_out), .D(entrada[0]), .Q(d_ff_86_q));  // open: Qn, preset, en, reset
  D_Flip_Flop d_ff_87 (.clk(and_15_out), .D(entrada[0]), .Q(d_ff_87_q));  // open: Qn, preset, en, reset
  D_Flip_Flop d_ff_88 (.clk(and_16_out), .D(entrada[0]), .Q(d_ff_88_q));  // open: Qn, preset, en, reset
  and and_98 (and_98_out, d_ff_82_q, and_2_out);
  and and_99 (and_99_out, d_ff_83_q, and_3_out);
  and and_100 (and_100_out, d_ff_84_q, and_4_out);
  and and_101 (and_101_out, d_ff_85_q, and_5_out);
  or or_11 (saida[0], and_97_out, and_98_out, and_99_out, and_100_out, and_101_out, and_102_out, and_103_out, and_104_out);
  and and_102 (and_102_out, d_ff_86_q, and_6_out);
  and and_103 (and_103_out, d_ff_87_q, and_7_out);
  and and_104 (and_104_out, d_ff_88_q, and_8_out);

  // Other names for the same wires on the sheet: numero[2:0] = selecao; _11 = saida[0]; _10 = saida[1]; _9 = saida[2];
  //   _8 = saida[3]; _7 = saida[4]; _6 = saida[5]; _5 = saida[6]; _4 = saida[7]; _3 = saida[8]; _2 = saida[9];
  //   _1 = saida[10]
endmodule

// subtrator
module somador_subtrator (
  input  [7:0] A,
  input  [7:0] B,
  input  C,
  output [7:0] S,
  output bit_extra
);

  wire and_1_out, and_2_out, and_3_out, and_4_out, and_5_out, and_6_out, and_7_out, and_8_out, and_9_out,
       and_10_out, and_11_out, and_12_out, and_13_out, and_14_out, and_15_out, and_16_out, and_17_out,
       and_18_out, and_19_out, and_20_out, and_21_out, and_22_out, and_23_out, and_24_out, and_25_out,
       and_26_out, and_27_out, and_28_out, B0, B1, B2, B3, B4, B5, B6, B7, G0, G1, G2, G3, G4, G5, G6, G7,
       or_1_out, or_2_out, or_3_out, or_4_out, or_5_out, or_6_out, or_7_out, P0, P1, P2, P3, P4, P5, P6, P7;

  assign {B7, B6, B5, B4, B3, B2, B1, B0} = B ^ {8{C}};  // XOR_Gate xor_1, 8 bits wide
  somador_1_bit somador_1_bit_1 (.S(S[0]), .A(A[0]), .B(B0), .Cin(C));
  and u_G0 (G0, A[0], B0);
  or u_P0 (P0, A[0], B0);
  somador_1_bit somador_1_bit_2 (.S(S[1]), .A(A[1]), .B(B1), .Cin(or_1_out));
  and u_G1 (G1, A[1], B1);
  or or_1 (or_1_out, G0, and_1_out);
  or u_P1 (P1, A[1], B1);
  and and_1 (and_1_out, P0, C);
  and and_2 (and_2_out, G0, P1);
  or or_2 (or_2_out, G1, and_2_out, and_3_out);
  somador_1_bit somador_1_bit_3 (.S(S[2]), .A(A[2]), .B(B2), .Cin(or_2_out));
  and u_G2 (G2, A[2], B2);
  and and_3 (and_3_out, P0, P1, C);
  or u_P2 (P2, A[2], B2);
  somador_1_bit somador_1_bit_4 (.S(S[3]), .A(A[3]), .B(B3), .Cin(or_3_out));
  and u_G3 (G3, A[3], B3);
  and and_4 (and_4_out, G1, P2);
  or or_3 (or_3_out, G2, and_4_out, and_5_out, and_6_out);
  or u_P3 (P3, A[3], B3);
  and and_5 (and_5_out, G0, P1, P2);
  and u_G4 (G4, A[4], B4);
  and and_6 (and_6_out, P0, P1, P2, C);
  or u_P4 (P4, A[4], B4);
  and and_7 (and_7_out, G2, P3);
  somador_1_bit somador_1_bit_5 (.S(S[4]), .A(A[4]), .B(B4), .Cin(or_4_out));
  and u_G5 (G5, A[5], B5);
  or or_4 (or_4_out, G3, and_7_out, and_8_out, and_9_out, and_10_out);
  or u_P5 (P5, A[5], B5);
  and and_8 (and_8_out, G1, P2, P3);
  and u_G6 (G6, A[6], B6);
  and and_9 (and_9_out, G0, P1, P2, P3);
  or u_P6 (P6, A[6], B6);
  and and_10 (and_10_out, P0, P1, P2, P3, C);
  and u_G7 (G7, A[7], B7);
  and and_11 (and_11_out, G3, P4);
  somador_1_bit somador_1_bit_6 (.S(S[5]), .A(A[5]), .B(B5), .Cin(or_5_out));
  or u_P7 (P7, A[7], B7);
  and and_12 (and_12_out, G2, P3, P4);
  or or_5 (or_5_out, G4, and_11_out, and_12_out, and_13_out, and_14_out, and_15_out);
  and and_13 (and_13_out, G1, P2, P3, P4);
  and and_14 (and_14_out, G0, P1, P2, P3, P4);
  and and_15 (and_15_out, P0, P1, P2, P3, P4, C);
  somador_1_bit somador_1_bit_7 (.S(S[6]), .A(A[6]), .B(B6), .Cin(or_6_out));
  and and_16 (and_16_out, G3, P4, P5);
  and and_17 (and_17_out, G4, P5);
  or or_6 (or_6_out, G5, and_17_out, and_16_out, and_18_out, and_19_out, and_20_out, and_21_out);
  and and_18 (and_18_out, G2, P3, P4, P5);
  and and_19 (and_19_out, G1, P2, P3, P4, P5);
  and and_20 (and_20_out, G0, P1, P2, P3, P4, P5);
  and and_21 (and_21_out, P0, P1, P2, P3, P4, P5, C);
  and and_22 (and_22_out, G5, P6);
  somador_1_bit somador_1_bit_8 (.S(bit_extra), .A(A[7]), .B(B7), .Cin(or_7_out));
  and and_23 (and_23_out, G4, P5, P6);
  and and_24 (and_24_out, G3, P4, P5, P6);
  or or_7 (or_7_out, G6, and_22_out, and_23_out, and_24_out, and_25_out, and_26_out, and_27_out, and_28_out);
  and and_25 (and_25_out, G2, P3, P4, P5, P6);
  and and_26 (and_26_out, G1, P2, P3, P4, P5, P6);
  and and_27 (and_27_out, G0, P1, P2, P3, P4, P5, P6);
  and and_28 (and_28_out, P0, P1, P2, P3, P4, P5, P6, C);

  assign S[7] = bit_extra;

  // Notes on the sheet:
  //   +
  //   =
endmodule

module somador_1_bit (
  input  A,
  input  B,
  input  Cin,
  output S
);

  wire xor_1_out;

  xor xor_1 (xor_1_out, Cin, B);
  xor xor_2 (S, xor_1_out, A);
endmodule

module selecao (
  input  [2:0] selecao,
  input  [10:0] entrada,
  input  ler_escrever,
  output [10:0] saida
);

  memoria_11_bits memoria_11_bits_1 (.saida(saida), .selecao(selecao), .entrada(entrada), .ler_escrever(ler_escrever));
endmodule

module ula (
  input  [7:0] a,
  input  [7:0] b,
  input  [2:0] operacao,
  output [7:0] saida,
  output [7:0] Resto_divisao,
  output [15:0] Resultado_multiplicacao
);

  wire [7:0] and_9_out, and_10_out, and_11_out, and_12_out, and_13_out, and_14_out, and_15_out, and_16_out,
       and_17_out, main_1_p4, not_out, or_out, somador_subtrator_1_s, somador_subtrator_2_s, xor_out;
  wire [7:7] and_1_out, and_2_out, and_3_out, and_4_out, and_5_out, and_6_out, and_7_out, and_8_out;

  and and_1 (and_1_out[7], ~operacao[2], ~operacao[1], ~operacao[0]);  // AND_Gate
  and and_2 (and_2_out[7], ~operacao[2], ~operacao[1], operacao[0]);  // AND_Gate
  and and_3 (and_3_out[7], ~operacao[2], operacao[1], ~operacao[0]);  // AND_Gate
  and and_4 (and_4_out[7], ~operacao[2], operacao[1], operacao[0]);  // AND_Gate
  and and_5 (and_5_out[7], operacao[2], ~operacao[1], ~operacao[0]);  // AND_Gate
  and and_6 (and_6_out[7], operacao[2], ~operacao[1], operacao[0]);  // AND_Gate
  and and_7 (and_7_out[7], operacao[2], operacao[1], ~operacao[0]);  // AND_Gate
  and and_8 (and_8_out[7], operacao[2], operacao[1], operacao[0]);
  // multiplicador multiplicador_1: pin names not known; wires that end beside it: b, a, Resultado_multiplicacao
  somador_subtrator somador_subtrator_1 (.A(a), .B(b), .S(somador_subtrator_1_s), .C(1'b0));  // open: bit_extra
  somador_subtrator somador_subtrator_2 (.A(b), .B(a), .S(somador_subtrator_2_s), .C(1'b1));  // open: bit_extra
  // divisor_8_bits_main main_1: pin names not known; wires that end beside it: b, Resto_divisao, a, main_1_p4
  assign and_9_out = a & b;  // AND_Gate and_9, 8 bits wide
  assign or_out = a | b;  // OR_Gate or, 8 bits wide
  assign not_out = ~a;  // NOT_Gate not, 8 bits wide
  assign xor_out = a ^ b;  // XOR_Gate xor, 8 bits wide
  assign and_10_out = somador_subtrator_1_s & {8{and_1_out[7]}};  // AND_Gate and_10, 8 bits wide
  assign and_11_out = somador_subtrator_2_s & {8{and_2_out[7]}};  // AND_Gate and_11, 8 bits wide
  assign and_12_out = main_1_p4 & {8{and_3_out[7]}};  // AND_Gate and_12, 8 bits wide
  assign and_13_out = Resultado_multiplicacao[7:0] & {8{and_4_out[7]}};  // AND_Gate and_13, 8 bits wide
  assign and_14_out = and_9_out & {8{and_5_out[7]}};  // AND_Gate and_14, 8 bits wide
  assign and_15_out = or_out & {8{and_6_out[7]}};  // AND_Gate and_15, 8 bits wide
  assign and_16_out = not_out & {8{and_7_out[7]}};  // AND_Gate and_16, 8 bits wide
  assign and_17_out = xor_out & {8{and_8_out[7]}};  // AND_Gate and_17, 8 bits wide
  assign saida = and_10_out | and_11_out | and_12_out | and_13_out | and_14_out | and_15_out | and_16_out | and_17_out;  // OR_Gate or_2, 8 bits wide

  // Other names for the same wires on the sheet: mult[15:0] = Resultado_multiplicacao;
  //   res_mult[7:0] = Resultado_multiplicacao[7:0]
endmodule

module acumulador (
  input  [7:0] entrada,
  input  ler_escrever,
  output [7:0] saida
);

  D_Flip_Flop d_ff_1 (.clk(ler_escrever), .D(entrada[7]), .Q(saida[7]));  // open: Qn, preset, en, reset
  D_Flip_Flop d_ff_2 (.clk(ler_escrever), .D(entrada[6]), .Q(saida[6]));  // open: Qn, preset, en, reset
  D_Flip_Flop d_ff_3 (.clk(ler_escrever), .D(entrada[5]), .Q(saida[5]));  // open: Qn, preset, en, reset
  D_Flip_Flop d_ff_4 (.clk(ler_escrever), .D(entrada[4]), .Q(saida[4]));  // open: Qn, preset, en, reset
  D_Flip_Flop d_ff_5 (.clk(ler_escrever), .D(entrada[3]), .Q(saida[3]));  // open: Qn, preset, en, reset
  D_Flip_Flop d_ff_6 (.clk(ler_escrever), .D(entrada[2]), .Q(saida[2]));  // open: Qn, preset, en, reset
  D_Flip_Flop d_ff_7 (.clk(ler_escrever), .D(entrada[1]), .Q(saida[1]));  // open: Qn, preset, en, reset
  D_Flip_Flop d_ff_8 (.clk(ler_escrever), .D(entrada[0]), .Q(saida[0]));  // open: Qn, preset, en, reset
endmodule

module contador (
  input  entrada,
  output [2:0] saida
);

  J_K_Flip_Flop #(.trigger("falling")) j_k_ff_1 (
    .J(1'b1), .clk(entrada), .K(1'b1), .Q(saida[0]));  // open: Qn, preset, en, reset
  J_K_Flip_Flop #(.trigger("falling")) j_k_ff_2 (
    .J(1'b1), .clk(saida[0]), .K(1'b1), .Q(saida[1]));  // open: Qn, preset, en, reset
  J_K_Flip_Flop #(.trigger("falling")) j_k_ff_3 (
    .J(1'b1), .clk(saida[1]), .K(1'b1), .Q(saida[2]));  // open: Qn, preset, en, reset
endmodule
